// Logisim project 8bit-cpu.circ as structural Verilog: 1 circuit, main circuit main
module main (
  input  in_1,
  input  in_2,
  input  in_3,
  input  in_4,
  input  in_5,
  input  in_6,
  input  in_7,
  input  in_8,
  input  in_9,
  input  in_10,
  input  in_11,
  input  in_12,
  input  in_13,
  input  in_14,
  input  in_15,
  input  in_16,
  input  in_17,
  input  in_18,
  input  in_19,
  input  in_20,
  input  in_21,
  input  in_22,
  input  in_23,
  input  in_24,
  input  in_25,
  input  in_26,
  input  in_27,
  input  in_28,
  input  in_29,
  input  in_30,
  input  in_31,
  input  in_32,
  input  in_33,
  input  in_34,
  input  in_35,
  input  in_36,
  input  in_37,
  input  in_38,
  input  in_39,
  input  in_40,
  input  in_41,
  input  in_42,
  input  in_43,
  input  in_44,
  input  in_45,
  input  in_46,
  input  in_47,
  input  in_48,
  input  in_49,
  input  in_50,
  input  in_51,
  input  in_52,
  input  in_53,
  input  in_54,
  input  in_55,
  input  in_56,
  input  in_57,
  input  in_58,
  input  in_59,
  input  in_60,
  input  in_61,
  input  in_62,
  input  in_63,
  input  in_64,
  input  in_65,
  input  in_66,
  input  in_67,
  input  in_68,
  input  in_69,
  input  in_70,
  input  in_71,
  input  in_72,
  input  in_73,
  input  in_74,
  input  in_75,
  input  in_76,
  input  in_77,
  input  in_78,
  input  in_79,
  input  in_80,
  input  in_81,
  input  in_82,
  input  in_83,
  input  in_84,
  input  in_85,
  input  in_86,
  input  in_87,
  input  in_88,
  input  in_89,
  input  in_90,
  input  in_91,
  input  in_92,
  input  in_93,
  input  in_94,
  input  in_95,
  input  in_96,
  input  in_97,
  input  in_98,
  input  in_99,
  input  in_100,
  input  in_101,
  input  in_102,
  input  in_103,
  input  in_104,
  input  in_105,
  input  in_106,
  input  in_107,
  input  in_108,
  input  in_109,
  input  in_110,
  input  in_111,
  input  in_112,
  input  in_113,
  input  in_114,
  input  in_115,
  input  in_116,
  input  in_117,
  input  in_118,
  input  in_119,
  input  in_120,
  input  in_121,
  input  in_122,
  input  in_123,
  input  in_124,
  input  in_125,
  input  in_126,
  input  in_127,
  input  in_128,
  input  in_129,
  input  in_130,
  input  in_131,
  input  in_132,
  input  in_133,
  input  in_134,
  input  in_135,
  input  in_136,
  input  in_137,
  input  in_138,
  input  in_139,
  input  in_140,
  input  in_141,
  input  in_142,
  input  in_143,
  input  in_144,
  input  in_145,
  input  in_146,
  input  in_147,
  input  in_148,
  input  in_149,
  input  in_150,
  input  in_151,
  input  in_152,
  input  in_153,
  input  in_154,
  input  in_155,
  input  in_156,
  input  in_157,
  input  in_158,
  input  in_159,
  input  in_160,
  input  in_161,
  input  in_162,
  input  in_163,
  input  in_164,
  input  in_165,
  input  in_166,
  input  in_167,
  input  in_168,
  input  in_169,
  input  in_170,
  input  in_171,
  input  RAM_selector,
  input  in_173,
  input  in_174,
  input  in_175,
  input  in_176,
  input  in_177,
  input  in_178,
  input  in_179,
  input  in_180,
  input  in_181,
  input  in_182,
  input  in_183,
  input  in_184,
  input  in_185,
  input  in_186,
  input  in_187,
  input  in_188,
  input  in_189,
  input  in_190,
  input  in_191,
  input  in_192,
  input  in_193,
  output out_194,
  output out_195,
  output out_196,
  output out_197,
  output out_198,
  output out_199,
  output out_200,
  output out_201,
  output out_202,
  output out_203,
  output out_204,
  output out_205,
  output out_206,
  output out_207,
  output out_208
);

  wire _00_1_en00, _00_1_out, _00_2_en00, _00_2_out, _00_3_en00, _00_3_out, _00_4_en00, _00_4_out,
       _00_5_en00, _00_5_out, _00_6_en00, _00_6_out, _00_7_en00, _00_7_out, _00_8_en00, _00_8_out,
       _01_1_en01, _01_1_out, _01_2_en01, _01_2_out, _01_3_en01, _01_3_out, _01_4_en01, _01_4_out,
       _01_5_en01, _01_5_out, _01_6_en01, _01_6_out, _01_7_en01, _01_7_out, _01_8_en01, _01_8_out, _1s_place,
       _02_1_en02, _02_1_out, _02_2_en02, _02_2_out, _02_3_en02, _02_3_out, _02_4_en02, _02_4_out,
       _02_5_en02, _02_5_out, _02_6_en02, _02_6_out, _02_7_en02, _02_7_out, _02_8_en02, _02_8_out, _2s_place,
       _03_1_en03, _03_1_out, _03_2_en03, _03_2_out, _03_3_en03, _03_3_out, _03_4_en03, _03_4_out,
       _03_5_en03, _03_5_out, _03_6_en03, _03_6_out, _03_7_en03, _03_7_out, _03_8_en03, _03_8_out,
       _04_1_en04, _04_1_out, _04_2_en04, _04_2_out, _04_3_en04, _04_3_out, _04_4_en04, _04_4_out,
       _04_5_en04, _04_5_out, _04_6_en04, _04_6_out, _04_7_en04, _04_7_out, _04_8_en04, _04_8_out, _4s_place,
       _05_1_en05, _05_1_out, _05_2_en05, _05_2_out, _05_3_en05, _05_3_out, _05_4_en05, _05_4_out,
       _05_5_en05, _05_5_out, _05_6_en05, _05_6_out, _05_7_en05, _05_7_out, _05_8_en05, _05_8_out,
       _06_1_en06, _06_1_out, _06_2_en06, _06_2_out, _06_3_en06, _06_3_out, _06_4_en06, _06_4_out,
       _06_5_en06, _06_5_out, _06_6_en06, _06_6_out, _06_7_en06, _06_7_out, _06_8_en06, _06_8_out,
       _07_1_en07, _07_1_out, _07_2_en07, _07_2_out, _07_3_en07, _07_3_out, _07_4_en07, _07_4_out,
       _07_5_en07, _07_5_out, _07_6_en07, _07_6_out, _07_7_en07, _07_7_out, _07_8_en07, _07_8_out,
       _08_1_en08, _08_1_out, _08_2_en08, _08_2_out, _08_3_en08, _08_3_out, _08_4_en08, _08_4_out,
       _08_5_en08, _08_5_out, _08_6_en08, _08_6_out, _08_7_en08, _08_7_out, _08_8_en08, _08_8_out, _8s_place,
       _09_1_en09, _09_1_out, _09_2_en09, _09_2_out, _09_3_en09, _09_3_out, _09_4_en09, _09_4_out,
       _09_5_en09, _09_5_out, _09_6_en09, _09_6_out, _09_7_en09, _09_7_out, _09_8_en09, _09_8_out,
       _10_1_en10, _10_1_out, _10_2_en10, _10_2_out, _10_3_en10, _10_3_out, _10_4_en10, _10_4_out,
       _10_5_en10, _10_5_out, _10_6_en10, _10_6_out, _10_7_en10, _10_7_out, _10_8_en10, _10_8_out,
       _11_1_en11, _11_1_out, _11_2_en11, _11_2_out, _11_3_en11, _11_3_out, _11_4_en11, _11_4_out,
       _11_5_en11, _11_5_out, _11_6_en11, _11_6_out, _11_7_en11, _11_7_out, _11_8_en11, _11_8_out,
       _12_1_en12, _12_1_out, _12_2_en12, _12_2_out, _12_3_en12, _12_3_out, _12_4_en12, _12_4_out,
       _12_5_en12, _12_5_out, _12_6_en12, _12_6_out, _12_7_en12, _12_7_out, _12_8_en12, _12_8_out,
       _13_1_en13, _13_1_out, _13_2_en13, _13_2_out, _13_3_en13, _13_3_out, _13_4_en13, _13_4_out,
       _13_5_en13, _13_5_out, _13_6_en13, _13_6_out, _13_7_en13, _13_7_out, _13_8_en13, _13_8_out,
       _14_1_en14, _14_1_out, _14_2_en14, _14_2_out, _14_3_en14, _14_3_out, _14_4_en14, _14_4_out,
       _14_5_en14, _14_5_out, _14_6_en14, _14_6_out, _14_7_en14, _14_7_out, _14_8_en14, _14_8_out,
       _15_1_en15, _15_1_out, _15_2_en15, _15_2_out, _15_3_en15, _15_3_out, _15_4_en15, _15_4_out,
       _15_5_en15, _15_5_out, _15_6_en15, _15_6_out, _15_7_en15, _15_7_out, _15_8_en15, _15_8_out,
       _16s_place, _32s_place, _64s_place, _128s_place, A1_loader_to_tristate, A1_out, A2_loader_to_tristate,
       A2_out, A3_loader_to_tristate, A3_out, A4_loader_to_tristate, A4_out, A5_loader_to_tristate, A5_out,
       A6_loader_to_tristate, A6_out, A7_loader_to_tristate, A7_out, A8_loader_to_tristate, A8_out,
       A_to_bus_out, ADD, add_or_subtract, add_or_subtract_out, adder_1_to_adder_2, adder_2_to_adder_3,
       adder_3_to_adder_4, adder_5_to_adder_6, adder_6_to_adder_7, adder_7_to_adder_8, and_1_out, and_2_out,
       and_3_out, and_4_out, and_5_out, and_6_out, and_7_out, and_8_out, and_9_out, and_10_out, and_11_out,
       and_12_out, and_13_out, and_14_out, and_15_out, and_16_out, and_17_out, and_18_out, and_19_out,
       and_20_out, and_21_out, and_22_out, and_23_out, and_24_out, and_25_out, and_26_out, and_27_out,
       and_28_out, and_29_out, and_30_out, and_31_out, and_32_out, and_33_out, and_34_out, and_35_out,
       and_36_out, and_37_out, and_38_out, and_39_out, and_40_out, and_41_out, and_42_out, and_43_out,
       and_44_out, and_45_out, and_46_out, and_47_out, and_48_out, and_49_out, and_50_out, and_51_out,
       and_52_out, and_53_out, and_54_out, and_55_out, and_56_out, and_57_out, and_58_out, and_59_out,
       and_60_out, and_61_out, and_62_out, and_63_out, and_64_out, and_65_out, and_66_out, and_67_out,
       and_68_out, and_69_out, and_70_out, and_71_out, and_72_out, and_73_out, and_74_out, and_75_out,
       and_76_out, and_77_out, and_78_out, and_79_out, and_80_out, and_81_out, and_82_out, and_83_out,
       and_84_out, and_85_out, and_86_out, and_87_out, and_88_out, and_89_out, and_90_out, and_91_out,
       and_92_out, and_93_out, and_94_out, and_95_out, and_96_out, and_97_out, and_98_out, and_99_out,
       and_100_out, and_101_out, and_102_out, and_103_out, and_104_out, and_105_out, and_106_out,
       and_107_out, and_108_out, and_109_out, and_110_out, and_111_out, and_112_out, and_113_out,
       and_114_out, and_115_out, and_116_out, and_117_out, and_118_out, and_119_out, and_120_out,
       and_121_out, and_122_out, and_123_out, and_124_out, and_125_out, and_126_out, and_127_out,
       and_128_out, and_129_out, and_130_out, and_131_out, and_132_out, and_133_out, and_134_out,
       and_135_out, and_136_out, and_137_out, and_142_out, and_148_out, and_149_out, and_150_out,
       and_151_out, and_152_out, and_153_out, and_154_out, and_155_out, and_156_out, and_157_out,
       and_158_out, and_159_out, and_160_out, and_161_out, and_162_out, and_163_out, and_164_out,
       and_165_out, and_166_out, and_167_out, and_168_out, and_169_out, and_170_out, and_171_out,
       and_172_out, and_173_out, and_174_out, and_175_out, and_176_out, and_177_out, and_178_out,
       and_179_out, and_180_out, and_181_out, and_182_out, and_183_out, and_184_out, and_185_out,
       and_186_out, and_187_out, and_188_out, and_189_out, and_190_out, and_191_out, and_192_out,
       and_193_out, and_194_out, and_195_out, and_196_out, and_197_out, and_198_out, and_199_out,
       and_200_out, and_201_out, and_202_out, and_203_out, and_204_out, and_205_out, and_206_out,
       and_207_out, and_208_out, and_209_out, and_210_out, and_211_out, and_212_out, and_213_out,
       and_214_out, and_215_out, and_216_out, and_217_out, and_218_out, and_219_out, and_224_out,
       and_225_out, and_226_out, and_227_out, and_228_out, and_229_out, and_230_out, and_231_out,
       and_233_out, and_234_out, and_235_out, and_239_out, and_240_out, and_241_out, and_242_out,
       and_243_out, and_244_out, and_245_out, and_246_out, and_247_out, and_248_out, and_249_out,
       and_250_out, and_251_out, and_252_out, and_253_out, and_254_out, and_255_out, and_256_out,
       and_257_out, and_258_out, and_259_out, and_260_out, and_261_out, and_262_out, and_263_out,
       and_264_out, and_265_out, and_266_out, and_267_out, and_268_out, and_269_out, and_270_out,
       and_271_out, and_272_out, and_273_out, and_274_out, and_275_out, and_276_out, and_277_out,
       and_278_out, and_279_out, and_280_out, and_281_out, and_282_out, and_283_out, and_284_out,
       and_285_out, and_286_out, and_287_out, and_288_out, and_289_out, and_290_out, and_291_out,
       and_292_out, and_293_out, and_294_out, and_295_out, and_296_out, and_297_out, and_298_out,
       and_299_out, and_300_out, and_301_out, and_302_out, and_303_out, and_304_out, and_305_out,
       and_306_out, and_307_out, and_308_out, and_314_out, and_315_out, and_316_out, and_317_out,
       and_318_out, and_319_out, and_320_out, and_321_out, and_322_out, and_323_out, and_324_out,
       and_325_out, and_326_out, and_327_out, and_328_out, and_329_out, and_330_out, and_331_out,
       and_332_out, and_333_out, and_334_out, and_335_out, and_336_out, and_337_out, and_338_out,
       and_339_out, and_340_out, and_341_out, and_342_out, and_343_out, and_344_out, and_345_out,
       and_346_out, and_347_out, and_348_out, and_349_out, and_350_out, and_351_out, and_352_out,
       and_353_out, and_354_out, and_355_out, and_356_out, and_357_out, and_358_out, and_359_out,
       and_360_out, and_361_out, and_362_out, and_363_out, and_364_out, and_365_out, and_366_out,
       and_367_out, and_368_out, and_369_out, and_370_out, and_371_out, and_372_out, and_373_out,
       and_374_out, and_375_out, and_376_out, and_377_out, and_382_out, and_383_out, and_384_out,
       and_385_out, and_386_out, and_387_out, and_388_out, and_389_out, and_390_out, and_391_out,
       and_392_out, and_393_out, and_394_out, and_395_out, and_396_out, and_397_out, and_398_out,
       and_399_out, and_400_out, and_401_out, and_402_out, and_403_out, and_404_out, and_405_out,
       and_406_out, and_407_out, and_408_out, and_409_out, and_410_out, and_411_out, and_412_out,
       and_413_out, and_414_out, and_415_out, and_416_out, and_417_out, and_418_out, and_419_out,
       and_420_out, and_421_out, and_422_out, and_423_out, and_424_out, and_425_out, and_426_out,
       and_427_out, and_428_out, and_429_out, and_430_out, and_431_out, and_432_out, and_433_out,
       and_434_out, and_435_out, and_436_out, and_437_out, and_438_out, and_439_out, and_440_out,
       and_441_out, and_442_out, and_443_out, and_444_out, and_445_out, and_446_out, and_447_out,
       and_448_out, and_449_out, and_450_out, and_451_out, and_484_out, and_485_out, and_486_out,
       and_487_out, and_488_out, and_489_out, and_490_out, and_491_out, and_492_out, and_493_out,
       and_495_out, and_496_out, and_498_out, and_499_out, and_500_out, and_502_out, and_503_out,
       and_504_out, and_506_out, and_507_out, and_540_out, and_541_out, and_543_out, and_544_out,
       and_546_out, and_547_out, and_548_out, and_550_out, and_551_out, and_552_out, and_554_out,
       and_555_out, and_556_out, and_557_out, and_558_out, and_559_out, and_560_out, and_561_out,
       and_562_out, and_563_out, and_564_out, and_565_out, and_566_out, and_567_out, and_568_out,
       and_569_out, and_570_out, and_571_out, and_572_out, and_573_out, and_574_out, and_575_out,
       and_576_out, and_577_out, and_578_out, and_579_out, and_580_out, and_581_out, and_582_out,
       and_583_out, and_584_out, and_585_out, and_586_out, and_587_out, and_588_out, and_589_out,
       and_590_out, and_591_out, and_592_out, and_593_out, and_594_out, and_595_out, and_596_out,
       and_597_out, and_598_out, and_599_out, and_600_out, and_601_out, and_602_out, and_603_out,
       and_604_out, and_605_out, and_606_out, and_607_out, and_608_out, and_609_out, and_613_out,
       and_614_out, and_616_out, and_617_out, and_619_out, and_620_out, and_622_out, and_623_out,
       and_625_out, and_626_out, and_627_out, and_628_out, and_629_out, and_630_out, and_631_out,
       and_632_out, and_633_out, and_634_out, and_635_out, and_636_out, and_637_out, and_638_out,
       and_639_out, and_640_out, and_641_out, and_642_out, and_643_out, and_644_out, and_645_out,
       and_646_out, and_647_out, and_648_out, and_649_out, and_650_out, and_651_out, and_652_out,
       and_653_out, and_654_out, and_655_out, and_656_out, and_657_out, and_658_out, and_659_out,
       and_660_out, and_661_out, and_662_out, and_663_out, and_664_out, and_665_out, and_666_out,
       and_667_out, and_668_out, and_669_out, and_670_out, and_672_out, and_673_out, and_675_out,
       and_676_out, and_677_out, and_679_out, and_680_out, and_682_out, and_683_out, and_685_out,
       and_686_out, and_688_out, and_689_out, and_690_out, and_691_out, and_692_out, and_693_out,
       and_694_out, and_695_out, and_696_out, and_697_out, and_698_out, and_699_out, and_700_out,
       and_701_out, and_702_out, and_703_out, and_704_out, and_705_out, and_706_out, and_707_out,
       and_708_out, and_709_out, and_710_out, and_711_out, and_712_out, and_713_out, and_714_out,
       and_715_out, and_716_out, and_717_out, and_718_out, and_719_out, and_720_out, and_721_out,
       and_722_out, and_723_out, and_724_out, and_725_out, and_726_out, and_727_out, and_728_out,
       and_729_out, and_730_out, and_731_out, and_732_out, and_733_out, and_734_out, and_735_out,
       and_736_out, and_737_out, and_738_out, and_739_out, and_740_out, and_741_out, and_742_out,
       and_743_out, and_744_out, and_745_out, and_746_out, and_747_out, and_748_out, and_749_out,
       and_750_out, and_751_out, and_752_out, and_753_out, and_754_out, and_755_out, and_756_out,
       and_757_out, and_758_out, and_759_out, and_760_out, and_761_out, and_762_out, and_763_out,
       and_764_out, and_765_out, and_766_out, and_767_out, and_768_out, and_769_out, and_770_out,
       and_771_out, and_773_out, and_775_out, and_776_out, and_778_out, and_779_out, and_781_out,
       and_782_out, and_783_out, and_784_out, and_785_out, and_786_out, and_787_out, and_788_out,
       and_789_out, and_790_out, and_791_out, and_792_out, and_793_out, and_794_out, and_795_out,
       and_796_out, and_797_out, and_798_out, and_799_out, and_800_out, and_801_out, and_802_out,
       and_803_out, and_804_out, and_805_out, and_806_out, and_807_out, and_808_out, and_809_out,
       and_810_out, and_811_out, and_812_out, and_813_out, and_814_out, and_815_out, and_816_out,
       and_817_out, and_818_out, and_819_out, and_820_out, and_821_out, and_822_out, and_823_out,
       and_824_out, and_825_out, and_826_out, and_827_out, and_828_out, and_829_out, and_830_out,
       and_831_out, and_832_out, and_833_out, and_834_out, and_835_out, and_836_out, and_837_out,
       and_838_out, and_839_out, and_840_out, and_841_out, and_842_out, and_843_out, and_845_out,
       and_846_out, and_847_out, and_849_out, and_850_out, and_852_out, and_853_out, and_855_out,
       and_856_out, and_857_out, and_858_out, and_859_out, and_860_out, and_861_out, and_862_out,
       and_863_out, and_864_out, and_865_out, and_866_out, and_867_out, and_868_out, and_869_out,
       and_870_out, and_871_out, and_872_out, and_873_out, and_874_out, and_875_out, and_876_out,
       and_877_out, and_878_out, and_879_out, and_880_out, and_881_out, and_882_out, and_883_out,
       and_884_out, and_885_out, and_886_out, and_887_out, and_888_out, and_889_out, and_890_out,
       and_891_out, and_892_out, and_893_out, and_894_out, and_896_out, and_897_out, and_898_out,
       and_900_out, and_901_out, and_902_out, and_903_out, and_904_out, and_905_out, and_906_out,
       and_907_out, and_908_out, and_909_out, and_910_out, and_911_out, and_912_out, and_913_out,
       and_914_out, and_915_out, and_916_out, and_917_out, and_918_out, and_919_out, and_920_out,
       and_921_out, and_922_out, and_923_out, and_924_out, and_925_out, and_926_out, and_927_out,
       and_928_out, and_929_out, and_930_out, and_931_out, and_932_out, and_933_out, and_934_out,
       and_935_out, and_936_out, and_937_out, and_938_out, and_939_out, and_940_out, and_941_out,
       and_942_out, and_943_out, and_944_out, and_945_out, and_946_out, and_948_out, and_950_out,
       and_951_out, and_952_out, and_953_out, and_954_out, and_955_out, and_988_out, and_989_out,
       and_991_out, and_992_out, and_994_out, and_995_out, and_996_out, and_998_out, and_999_out,
       and_1000_out, and_1002_out, and_1003_out, and_1005_out, and_1006_out, and_1007_out, and_1040_out,
       and_1041_out, and_1042_out, and_1043_out, and_1044_out, and_1045_out, and_1046_out, and_1047_out,
       and_1048_out, and_1049_out, and_1050_out, and_1051_out, and_1052_out, and_1053_out, and_1054_out,
       and_1055_out, and_1056_out, and_1057_out, and_1058_out, and_1059_out, and_1060_out, and_1061_out,
       and_1062_out, and_1063_out, and_1064_out, and_1065_out, and_1066_out, and_1067_out, and_1068_out,
       and_1069_out, and_1070_out, and_1071_out, and_1072_out, and_1073_out, and_1074_out, and_1075_out,
       and_1076_out, and_1077_out, and_1079_out, and_1080_out, and_1081_out, and_1082_out, and_1083_out,
       and_1085_out, and_1086_out, and_1087_out, and_1088_out, and_1089_out, and_1090_out, B1_inverter,
       B1_out, B2_inverter, B2_out, B3_inverter, B3_out, B4_inverter, B4_out, B5_inverter, B5_out,
       B6_inverter, B6_out, B7_inverter, B7_out, B8_inverter, B8_out, bus_to_A, bus_to_A_out, bus_to_B,
       bus_to_B_out, bus_to_IR, bus_to_IR_out, bus_to_mem, bus_to_mem_out, bus_to_ram, bus_to_ram_out,
       carry_out, carry_out_to_inverter, counter_in, counter_to_bus, en00, en01, en02, en03, en04, en05,
       en06, en07, en08, en09, en10, en11, en12, en13, en14, en15, halt, increment_PC, IR_1_out, IR_2_out,
       IR_3_out, IR_4_out, IR_5_out, IR_6_out, IR_7_out, IR_8_out, IR_to_bus, IR_to_bus_out, LDA, M0_out,
       M1_out, M2_out, M3_out, MC_0_halter, MC_0_mux, MC_1_halter, MC_1_mux, MC_2_halter, MC_2_mux, MC_reset,
       NA0, NA1, NA2, NA3, nor_1_out, nor_2_out, not_1_out, not_2_out, not_3_out, not_4_out, not_5_out,
       not_6_out, not_7_out, not_8_out, not_9_out, not_10_out, not_11_out, not_12_out, not_13_out,
       not_14_out, not_15_out, not_16_out, not_17_out, not_18_out, not_19_out, not_20_out, not_21_out,
       not_22_out, not_23_out, not_24_out, not_25_out, not_26_out, not_27_out, not_28_out, not_29_out,
       not_30_out, not_31_out, not_32_out, not_33_out, not_34_out, not_35_out, not_36_out, not_37_out,
       not_38_out, not_39_out, not_40_out, not_41_out, not_42_out, not_43_out, not_44_out, not_45_out,
       not_46_out, not_47_out, not_48_out, not_49_out, not_50_out, not_51_out, not_56_out, not_57_out,
       not_58_out, not_59_out, not_60_out, not_61_out, not_62_out, not_63_out, not_64_out, not_65_out,
       not_66_out, not_67_out, not_68_out, not_69_out, not_70_out, not_71_out, not_72_out, not_73_out,
       not_74_out, not_75_out, not_76_out, not_77_out, not_78_out, not_79_out, not_80_out, not_81_out,
       not_82_out, not_83_out, not_84_out, not_85_out, not_86_out, not_87_out, not_88_out, not_89_out,
       not_90_out, not_91_out, not_92_out, not_93_out, not_94_out, not_95_out, not_96_out, not_97_out,
       not_98_out, not_99_out, not_100_out, not_101_out, not_102_out, not_103_out, not_104_out, not_105_out,
       not_106_out, not_107_out, not_108_out, not_109_out, not_110_out, not_111_out, not_112_out,
       not_113_out, not_114_out, not_115_out, not_116_out, not_117_out, not_118_out, not_119_out,
       not_120_out, not_121_out, not_122_out, not_123_out, not_124_out, not_125_out, not_126_out,
       not_127_out, not_128_out, not_129_out, not_130_out, not_131_out, not_132_out, not_133_out,
       not_134_out, not_135_out, not_136_out, not_137_out, not_138_out, not_139_out, not_140_out,
       not_141_out, not_142_out, not_143_out, not_144_out, not_145_out, not_146_out, not_147_out,
       not_148_out, not_149_out, not_150_out, not_151_out, not_152_out, not_153_out, not_154_out,
       not_155_out, not_156_out, not_157_out, not_158_out, not_159_out, not_160_out, not_161_out,
       not_162_out, not_163_out, not_164_out, not_165_out, not_166_out, not_167_out, not_168_out,
       not_169_out, not_170_out, not_171_out, not_172_out, not_173_out, not_174_out, not_175_out,
       not_176_out, not_177_out, not_178_out, not_179_out, not_180_out, not_181_out, not_182_out,
       not_183_out, not_184_out, not_185_out, not_186_out, not_187_out, not_188_out, not_189_out,
       not_190_out, not_191_out, not_192_out, not_193_out, not_194_out, not_195_out, not_196_out,
       not_197_out, not_198_out, not_199_out, not_200_out, not_201_out, not_202_out, not_203_out,
       not_204_out, not_205_out, not_206_out, not_207_out, not_208_out, not_209_out, not_210_out,
       not_211_out, not_212_out, not_213_out, not_214_out, not_215_out, not_216_out, not_217_out,
       not_218_out, not_219_out, not_220_out, not_221_out, not_222_out, not_223_out, not_224_out,
       not_225_out, not_226_out, not_227_out, not_228_out, not_229_out, not_230_out, not_231_out,
       not_232_out, not_233_out, not_234_out, not_235_out, not_236_out, not_237_out, not_238_out,
       not_239_out, not_240_out, not_241_out, not_242_out, not_243_out, not_244_out, not_245_out,
       not_246_out, not_247_out, not_248_out, not_249_out, not_250_out, not_251_out, not_252_out,
       not_253_out, not_254_out, not_255_out, not_256_out, not_257_out, not_258_out, not_259_out,
       not_260_out, not_261_out, not_262_out, not_263_out, not_265_out, not_266_out, not_267_out,
       not_268_out, not_269_out, not_270_out, not_271_out, not_272_out, not_273_out, not_274_out,
       not_275_out, not_276_out, not_277_out, not_278_out, not_279_out, not_280_out, not_281_out,
       not_282_out, not_283_out, not_284_out, not_285_out, not_286_out, not_287_out, not_288_out,
       not_289_out, not_290_out, not_291_out, not_292_out, not_293_out, not_294_out, not_295_out,
       not_296_out, not_297_out, not_298_out, not_299_out, not_300_out, not_301_out, not_302_out,
       not_303_out, not_304_out, not_305_out, not_306_out, not_307_out, not_308_out, not_309_out,
       not_310_out, not_311_out, not_312_out, not_313_out, not_314_out, not_315_out, not_316_out,
       not_317_out, not_318_out, not_319_out, not_320_out, not_321_out, not_322_out, not_323_out,
       not_324_out, not_325_out, not_326_out, not_327_out, not_328_out, not_329_out, not_330_out,
       not_331_out, not_332_out, not_333_out, not_334_out, not_335_out, not_336_out, not_337_out,
       not_338_out, not_339_out, not_340_out, not_341_out, not_342_out, not_343_out, not_344_out,
       not_345_out, not_346_out, not_347_out, not_348_out, not_349_out, not_350_out, not_351_out,
       not_352_out, not_353_out, not_354_out, not_355_out, not_356_out, not_357_out, not_358_out,
       not_359_out, not_360_out, not_361_out, not_362_out, not_363_out, not_364_out, not_365_out,
       not_366_out, not_367_out, not_368_out, not_369_out, not_370_out, not_371_out, not_372_out,
       not_373_out, not_374_out, not_375_out, not_376_out, not_377_out, not_378_out, not_379_out,
       not_380_out, not_381_out, not_382_out, not_383_out, not_384_out, not_385_out, not_386_out,
       not_387_out, not_388_out, not_389_out, not_390_out, not_391_out, not_392_out, not_393_out,
       not_394_out, not_395_out, not_396_out, not_397_out, not_398_out, not_399_out, not_400_out,
       not_401_out, not_402_out, not_403_out, not_404_out, not_405_out, not_406_out, not_407_out,
       not_408_out, or_1_out, or_2_out, or_3_out, or_4_out, or_5_out, or_6_out, or_7_out, or_8_out,
       or_35_out, or_37_out, or_39_out, or_41_out, or_43_out, or_45_out, or_47_out, or_49_out, or_51_out,
       or_52_out, or_53_out, or_54_out, or_55_out, or_56_out, or_57_out, or_58_out, or_60_out, or_61_out,
       or_62_out, or_63_out, or_76_out, or_222_out, or_223_out, or_224_out, or_225_out, or_226_out,
       or_227_out, or_228_out, or_229_out, or_230_out, or_231_out, or_232_out, or_233_out, or_234_out,
       or_235_out, or_236_out, or_237_out, or_238_out, or_239_out, or_240_out, or_241_out, or_242_out,
       or_243_out, or_244_out, or_245_out, or_246_out, or_247_out, or_248_out, or_249_out, or_250_out,
       or_251_out, or_252_out, or_253_out, or_254_out, or_255_out, or_256_out, or_257_out, or_258_out,
       or_259_out, or_260_out, or_261_out, or_262_out, or_263_out, or_264_out, or_265_out, or_266_out,
       or_267_out, or_268_out, or_269_out, or_270_out, or_271_out, or_272_out, or_273_out, or_274_out,
       or_275_out, or_276_out, or_277_out, or_278_out, or_280_out, or_282_out, or_284_out, or_286_out,
       or_288_out, or_290_out, or_292_out, or_297_out, or_298_out, or_299_out, or_300_out, or_301_out,
       or_302_out, or_303_out, or_304_out, or_305_out, or_306_out, or_307_out, or_308_out, or_309_out,
       or_310_out, or_311_out, or_312_out, or_317_out, or_318_out, or_319_out, or_320_out, or_321_out,
       or_322_out, or_323_out, or_324_out, or_325_out, or_326_out, or_327_out, or_328_out, or_329_out,
       or_330_out, or_331_out, or_332_out, or_333_out, or_334_out, or_335_out, or_336_out, or_337_out,
       or_338_out, or_339_out, or_340_out, or_341_out, or_342_out, or_343_out, or_344_out, or_345_out,
       or_346_out, or_347_out, or_348_out, or_356_out, or_359_out, PC_0_mux, PC_0_mux_2, PC_1_mux,
       PC_1_mux_2, PC_2_mux, PC_2_mux_2, PC_3_mux, PC_3_mux_2, ram_1, ram_2, ram_3, ram_4, ram_5, ram_6,
       ram_7, ram_8, ram_to_bus, ram_to_bus_1, ram_to_bus_2, ram_to_bus_3, ram_to_bus_4, ram_to_bus_5,
       ram_to_bus_6, ram_to_bus_7, ram_to_bus_8, ram_to_bus_out, reg_A_to_bus, run_alu, run_alu_out, T0, T1,
       T2, T3, tristate_A_to_adder_1, tristate_A_to_adder_2, tristate_A_to_adder_3, tristate_A_to_adder_4,
       tristate_A_to_adder_5, tristate_A_to_adder_6, tristate_A_to_adder_7, tristate_A_to_adder_8,
       tristate_B_to_adder_1, tristate_B_to_adder_2, tristate_B_to_adder_3, tristate_B_to_adder_4,
       tristate_B_to_adder_5, tristate_B_to_adder_6, tristate_B_to_adder_7, tristate_B_to_adder_8, wr00,
       wr01, wr02, wr03, wr04, wr05, wr06, wr07, wr08, wr09, wr10, wr11, wr12, wr13, wr14, wr15, xnor_1_out,
       xor_1_out, xor_2_out, xor_3_out, xor_4_out, xor_5_out, xor_6_out, xor_7_out, xor_8_out, xor_9_out,
       xor_10_out, xor_11_out, xor_12_out, xor_13_out, xor_15_out, xor_17_out, xor_19_out, xor_21_out,
       xor_22_out, xor_23_out, xor_24_out, xor_26_out, xor_28_out, xor_30_out, xor_32_out;

  xor xor_1 (xor_1_out, in_49, in_49);
  not not_1 (not_1_out, ram_to_bus);
  and and_1 (and_1_out, xor_1_out, not_1_out);
  not not_2 (not_2_out, bus_to_A);
  not not_3 (not_3_out, bus_to_A);
  not not_4 (not_4_out, bus_to_A);
  not not_5 (not_5_out, bus_to_A);
  not not_6 (not_6_out, bus_to_A);
  not not_7 (not_7_out, bus_to_A);
  not not_8 (not_8_out, bus_to_A);
  not not_9 (not_9_out, bus_to_A);
  not not_10 (not_10_out, bus_to_B);
  not not_11 (not_11_out, bus_to_B);
  not not_12 (not_12_out, bus_to_B);
  not not_13 (not_13_out, bus_to_B);
  not not_14 (not_14_out, bus_to_B);
  not not_15 (not_15_out, bus_to_B);
  not not_16 (not_16_out, bus_to_B);
  not not_17 (not_17_out, bus_to_B);
  not not_18 (not_18_out, run_alu);
  not not_19 (not_19_out, run_alu);
  not not_20 (not_20_out, run_alu);
  not not_21 (not_21_out, run_alu);
  not not_22 (not_22_out, run_alu);
  not not_23 (not_23_out, run_alu);
  not not_24 (not_24_out, run_alu);
  not not_25 (not_25_out, run_alu);
  not not_26 (not_26_out, reg_A_to_bus);
  and and_2 (and_2_out, not_26_out, IR_1_out);
  and and_3 (and_3_out, A1_out, reg_A_to_bus);
  or or_1 (or_1_out, and_3_out, and_2_out);
  not not_27 (not_27_out, reg_A_to_bus);
  and and_4 (and_4_out, not_27_out, IR_2_out);
  and and_5 (and_5_out, A2_out, reg_A_to_bus);
  or or_2 (or_2_out, and_5_out, and_4_out);
  not not_28 (not_28_out, reg_A_to_bus);
  and and_6 (and_6_out, not_28_out, IR_3_out);
  and and_7 (and_7_out, A3_out, reg_A_to_bus);
  or or_3 (or_3_out, and_7_out, and_6_out);
  not not_29 (not_29_out, reg_A_to_bus);
  and and_8 (and_8_out, A4_out, reg_A_to_bus);
  and and_9 (and_9_out, not_29_out, IR_4_out);
  or or_4 (or_4_out, and_8_out, and_9_out);
  not not_30 (not_30_out, reg_A_to_bus);
  and and_10 (and_10_out, not_30_out, IR_5_out);
  and and_11 (and_11_out, A5_out, reg_A_to_bus);
  or or_5 (or_5_out, and_11_out, and_10_out);
  not not_31 (not_31_out, reg_A_to_bus);
  and and_12 (and_12_out, not_31_out, IR_6_out);
  and and_13 (and_13_out, A6_out, reg_A_to_bus);
  or or_6 (or_6_out, and_13_out, and_12_out);
  not not_32 (not_32_out, reg_A_to_bus);
  and and_14 (and_14_out, A7_out, reg_A_to_bus);
  and and_15 (and_15_out, not_32_out, IR_7_out);
  or or_7 (or_7_out, and_14_out, and_15_out);
  not not_33 (not_33_out, reg_A_to_bus);
  and and_16 (and_16_out, A8_out, reg_A_to_bus);
  and and_17 (and_17_out, not_33_out, IR_8_out);
  or or_8 (or_8_out, and_16_out, and_17_out);
  and and_18 (and_18_out, ram_to_bus, ram_8);
  or or_9 (ram_to_bus_8, and_1_out, and_18_out);
  and and_19 (and_19_out, out_201, bus_to_A);
  and and_20 (and_20_out, not_2_out, in_99);
  and and_21 (and_21_out, out_200, bus_to_A);
  and and_22 (and_22_out, not_3_out, in_98);
  and and_23 (and_23_out, out_199, bus_to_A);
  and and_24 (and_24_out, not_4_out, in_97);
  and and_25 (and_25_out, out_198, bus_to_A);
  and and_26 (and_26_out, not_5_out, in_96);
  and and_27 (and_27_out, out_197, bus_to_A);
  and and_28 (and_28_out, not_6_out, in_95);
  and and_29 (and_29_out, out_196, bus_to_A);
  and and_30 (and_30_out, not_7_out, in_94);
  and and_31 (and_31_out, out_195, bus_to_A);
  and and_32 (and_32_out, not_8_out, in_93);
  and and_33 (and_33_out, out_194, bus_to_A);
  and and_34 (and_34_out, not_9_out, in_92);
  and and_35 (and_35_out, out_201, bus_to_B);
  and and_36 (and_36_out, not_10_out, in_115);
  and and_37 (and_37_out, out_200, bus_to_B);
  and and_38 (and_38_out, not_11_out, in_114);
  and and_39 (and_39_out, out_199, bus_to_B);
  and and_40 (and_40_out, not_12_out, in_113);
  and and_41 (and_41_out, out_198, bus_to_B);
  and and_42 (and_42_out, not_13_out, in_112);
  and and_43 (and_43_out, out_197, bus_to_B);
  and and_44 (and_44_out, not_14_out, in_111);
  and and_45 (and_45_out, out_196, bus_to_B);
  and and_46 (and_46_out, not_15_out, in_110);
  and and_47 (and_47_out, out_195, bus_to_B);
  and and_48 (and_48_out, not_16_out, in_109);
  and and_49 (and_49_out, out_194, bus_to_B);
  and and_50 (and_50_out, not_17_out, in_108);
  and and_51 (and_51_out, _1s_place, run_alu);
  and and_52 (and_52_out, not_18_out, A1_loader_to_tristate);
  and and_53 (and_53_out, _2s_place, run_alu);
  and and_54 (and_54_out, not_19_out, A2_loader_to_tristate);
  and and_55 (and_55_out, _4s_place, run_alu);
  and and_56 (and_56_out, not_20_out, A3_loader_to_tristate);
  and and_57 (and_57_out, _8s_place, run_alu);
  and and_58 (and_58_out, not_21_out, A4_loader_to_tristate);
  and and_59 (and_59_out, _16s_place, run_alu);
  and and_60 (and_60_out, not_22_out, A5_loader_to_tristate);
  and and_61 (and_61_out, _32s_place, run_alu);
  and and_62 (and_62_out, not_23_out, A6_loader_to_tristate);
  and and_63 (and_63_out, _64s_place, run_alu);
  or or_10 (A7_out, and_63_out, and_64_out);
  and and_64 (and_64_out, not_24_out, A7_loader_to_tristate);
  and and_65 (and_65_out, _128s_place, run_alu);
  or or_11 (A8_out, and_65_out, and_66_out);
  and and_66 (and_66_out, not_25_out, A8_loader_to_tristate);
  and and_67 (and_67_out, or_1_out, or_35_out);
  and and_68 (and_68_out, or_2_out, or_37_out);
  and and_69 (and_69_out, or_3_out, or_39_out);
  and and_70 (and_70_out, or_4_out, or_41_out);
  and and_71 (and_71_out, or_5_out, or_43_out);
  and and_72 (and_72_out, or_6_out, or_45_out);
  and and_73 (and_73_out, or_7_out, or_47_out);
  and and_74 (and_74_out, or_8_out, or_49_out);
  not not_34 (not_34_out, ram_to_bus);
  xor xor_2 (xor_2_out, in_50, in_50);
  and and_75 (and_75_out, xor_2_out, not_34_out);
  or or_12 (ram_to_bus_7, and_75_out, and_84_out);
  or or_13 (A1_loader_to_tristate, and_19_out, and_20_out);
  or or_14 (A2_loader_to_tristate, and_21_out, and_22_out);
  or or_15 (A3_loader_to_tristate, and_23_out, and_24_out);
  or or_16 (A4_loader_to_tristate, and_25_out, and_26_out);
  or or_17 (A5_loader_to_tristate, and_27_out, and_28_out);
  or or_18 (A6_loader_to_tristate, and_29_out, and_30_out);
  or or_19 (A7_loader_to_tristate, and_31_out, and_32_out);
  or or_20 (A8_loader_to_tristate, and_33_out, and_34_out);
  or or_21 (B1_inverter, and_35_out, and_36_out);
  or or_22 (B2_inverter, and_37_out, and_38_out);
  or or_23 (B3_inverter, and_39_out, and_40_out);
  or or_24 (B4_inverter, and_41_out, and_42_out);
  or or_25 (B5_inverter, and_43_out, and_44_out);
  or or_26 (B6_inverter, and_45_out, and_46_out);
  or or_27 (B7_inverter, and_47_out, and_48_out);
  or or_28 (B8_inverter, and_49_out, and_50_out);
  or or_29 (A1_out, and_51_out, and_52_out);
  or or_30 (A2_out, and_53_out, and_54_out);
  or or_31 (A3_out, and_55_out, and_56_out);
  or or_32 (A4_out, and_57_out, and_58_out);
  or or_33 (A5_out, and_59_out, and_60_out);
  or or_34 (A6_out, and_61_out, and_62_out);
  or or_35 (or_35_out, IR_to_bus, reg_A_to_bus);
  not not_35 (not_35_out, or_35_out);
  and and_76 (and_76_out, not_35_out, or_51_out);
  or or_36 (out_201, and_67_out, and_76_out);
  or or_37 (or_37_out, IR_to_bus, reg_A_to_bus);
  not not_36 (not_36_out, or_37_out);
  and and_77 (and_77_out, not_36_out, or_52_out);
  or or_38 (out_200, and_68_out, and_77_out);
  or or_39 (or_39_out, IR_to_bus, reg_A_to_bus);
  not not_37 (not_37_out, or_39_out);
  and and_78 (and_78_out, not_37_out, or_53_out);
  or or_40 (out_199, and_69_out, and_78_out);
  or or_41 (or_41_out, IR_to_bus, reg_A_to_bus);
  not not_38 (not_38_out, or_41_out);
  and and_79 (and_79_out, not_38_out, or_54_out);
  or or_42 (out_198, and_70_out, and_79_out);
  or or_43 (or_43_out, IR_to_bus, reg_A_to_bus);
  not not_39 (not_39_out, or_43_out);
  and and_80 (and_80_out, not_39_out, or_55_out);
  or or_44 (out_197, and_71_out, and_80_out);
  or or_45 (or_45_out, IR_to_bus, reg_A_to_bus);
  not not_40 (not_40_out, or_45_out);
  and and_81 (and_81_out, not_40_out, or_56_out);
  or or_46 (out_196, and_72_out, and_81_out);
  or or_47 (or_47_out, IR_to_bus, reg_A_to_bus);
  not not_41 (not_41_out, or_47_out);
  and and_82 (and_82_out, not_41_out, or_57_out);
  or or_48 (out_195, and_73_out, and_82_out);
  or or_49 (or_49_out, IR_to_bus, reg_A_to_bus);
  not not_42 (not_42_out, or_49_out);
  and and_83 (and_83_out, not_42_out, or_58_out);
  or or_50 (out_194, and_74_out, and_83_out);
  and and_84 (and_84_out, ram_to_bus, ram_7);
  not not_43 (not_43_out, ram_to_bus);
  and and_85 (and_85_out, not_43_out, or_60_out);
  and and_86 (and_86_out, ram_to_bus_1, ram_to_bus);
  or or_51 (or_51_out, and_86_out, and_85_out);
  not not_44 (not_44_out, ram_to_bus);
  and and_87 (and_87_out, ram_to_bus_2, ram_to_bus);
  and and_88 (and_88_out, not_44_out, or_61_out);
  or or_52 (or_52_out, and_87_out, and_88_out);
  not not_45 (not_45_out, ram_to_bus);
  and and_89 (and_89_out, ram_to_bus_3, ram_to_bus);
  and and_90 (and_90_out, not_45_out, or_62_out);
  or or_53 (or_53_out, and_89_out, and_90_out);
  not not_46 (not_46_out, ram_to_bus);
  and and_91 (and_91_out, not_46_out, or_63_out);
  and and_92 (and_92_out, ram_to_bus_4, ram_to_bus);
  or or_54 (or_54_out, and_92_out, and_91_out);
  not not_47 (not_47_out, ram_to_bus);
  and and_93 (and_93_out, ram_to_bus_5, ram_to_bus);
  and and_94 (and_94_out, not_47_out, xor_4_out);
  or or_55 (or_55_out, and_93_out, and_94_out);
  not not_48 (not_48_out, ram_to_bus);
  and and_95 (and_95_out, ram_to_bus_6, ram_to_bus);
  and and_96 (and_96_out, not_48_out, xor_5_out);
  or or_56 (or_56_out, and_95_out, and_96_out);
  not not_49 (not_49_out, ram_to_bus);
  and and_97 (and_97_out, ram_to_bus_7, ram_to_bus);
  and and_98 (and_98_out, not_49_out, xor_6_out);
  or or_57 (or_57_out, and_97_out, and_98_out);
  not not_50 (not_50_out, ram_to_bus);
  and and_99 (and_99_out, not_50_out, xor_7_out);
  and and_100 (and_100_out, ram_to_bus_8, ram_to_bus);
  or or_58 (or_58_out, and_100_out, and_99_out);
  xor xor_3 (xor_3_out, in_51, in_51);
  not not_51 (not_51_out, ram_to_bus);
  and and_101 (and_101_out, xor_3_out, not_51_out);
  or or_59 (ram_to_bus_6, and_101_out, and_102_out);
  xor xor_4 (xor_4_out, in_183, in_183);
  xor xor_5 (xor_5_out, in_184, in_184);
  xor xor_6 (xor_6_out, in_185, in_185);
  xor xor_7 (xor_7_out, in_188, in_188);
  and and_102 (and_102_out, ram_to_bus, ram_6);
  not not_52 (NA3, RAM_selector);
  not not_53 (NA2, in_174);
  not not_54 (NA1, in_177);
  not not_55 (NA0, in_178);
  not not_56 (not_56_out, B1_inverter);
  and and_103 (and_103_out, not_56_out, add_or_subtract);
  not not_57 (not_57_out, add_or_subtract);
  and and_104 (and_104_out, not_57_out, B1_inverter);
  not not_58 (not_58_out, B2_inverter);
  and and_105 (and_105_out, not_58_out, add_or_subtract);
  not not_59 (not_59_out, add_or_subtract);
  and and_106 (and_106_out, not_59_out, B2_inverter);
  not not_60 (not_60_out, B3_inverter);
  and and_107 (and_107_out, not_60_out, add_or_subtract);
  not not_61 (not_61_out, add_or_subtract);
  and and_108 (and_108_out, not_61_out, B3_inverter);
  not not_62 (not_62_out, B4_inverter);
  and and_109 (and_109_out, not_62_out, add_or_subtract);
  not not_63 (not_63_out, add_or_subtract);
  and and_110 (and_110_out, not_63_out, B4_inverter);
  not not_64 (not_64_out, B5_inverter);
  and and_111 (and_111_out, not_64_out, add_or_subtract);
  not not_65 (not_65_out, add_or_subtract);
  and and_112 (and_112_out, not_65_out, B5_inverter);
  not not_66 (not_66_out, B6_inverter);
  and and_113 (and_113_out, not_66_out, add_or_subtract);
  not not_67 (not_67_out, add_or_subtract);
  and and_114 (and_114_out, not_67_out, B6_inverter);
  not not_68 (not_68_out, B7_inverter);
  and and_115 (and_115_out, not_68_out, add_or_subtract);
  not not_69 (not_69_out, add_or_subtract);
  and and_116 (and_116_out, not_69_out, B7_inverter);
  not not_70 (not_70_out, B8_inverter);
  and and_117 (and_117_out, not_70_out, add_or_subtract);
  not not_71 (not_71_out, add_or_subtract);
  and and_118 (and_118_out, not_71_out, B8_inverter);
  not not_72 (not_72_out, counter_to_bus);
  and and_119 (and_119_out, out_205, counter_to_bus);
  and and_120 (and_120_out, not_72_out, xor_9_out);
  or or_60 (or_60_out, and_119_out, and_120_out);
  not not_73 (not_73_out, counter_to_bus);
  and and_121 (and_121_out, not_73_out, xor_10_out);
  and and_122 (and_122_out, out_204, counter_to_bus);
  or or_61 (or_61_out, and_122_out, and_121_out);
  not not_74 (not_74_out, counter_to_bus);
  and and_123 (and_123_out, not_74_out, xor_11_out);
  and and_124 (and_124_out, out_203, counter_to_bus);
  or or_62 (or_62_out, and_124_out, and_123_out);
  not not_75 (not_75_out, counter_to_bus);
  and and_125 (and_125_out, not_75_out, xor_12_out);
  and and_126 (and_126_out, out_202, counter_to_bus);
  or or_63 (or_63_out, and_126_out, and_125_out);
  not not_76 (not_76_out, ram_to_bus);
  xor xor_8 (xor_8_out, in_52, in_52);
  and and_127 (and_127_out, xor_8_out, not_76_out);
  or or_64 (ram_to_bus_5, and_127_out, and_128_out);
  or or_65 (B1_out, and_103_out, and_104_out);
  or or_66 (B2_out, and_105_out, and_106_out);
  or or_67 (B3_out, and_107_out, and_108_out);
  or or_68 (B4_out, and_109_out, and_110_out);
  or or_69 (B5_out, and_111_out, and_112_out);
  or or_70 (B6_out, and_113_out, and_114_out);
  or or_71 (B7_out, and_115_out, and_116_out);
  or or_72 (B8_out, and_117_out, and_118_out);
  buf xor_9 (xor_9_out, in_179);  // XOR_Gate
  buf xor_10 (xor_10_out, in_180);  // XOR_Gate
  buf xor_11 (xor_11_out, in_181);  // XOR_Gate
  buf xor_12 (xor_12_out, in_182);  // XOR_Gate
  and and_128 (and_128_out, ram_to_bus, ram_5);
  and and_129 (and_129_out, add_or_subtract, tristate_A_to_adder_1);
  xor xor_13 (xor_13_out, add_or_subtract, tristate_A_to_adder_1);
  or or_73 (adder_1_to_adder_2, and_129_out, and_130_out);
  and and_130 (and_130_out, xor_13_out, tristate_B_to_adder_1);
  xor xor_14 (_1s_place, xor_13_out, tristate_B_to_adder_1);
  and and_131 (and_131_out, adder_1_to_adder_2, tristate_A_to_adder_2);
  xor xor_15 (xor_15_out, adder_1_to_adder_2, tristate_A_to_adder_2);
  or or_74 (adder_2_to_adder_3, and_131_out, and_132_out);
  and and_132 (and_132_out, xor_15_out, tristate_B_to_adder_2);
  xor xor_16 (_2s_place, xor_15_out, tristate_B_to_adder_2);
  and and_133 (and_133_out, adder_2_to_adder_3, tristate_A_to_adder_3);
  xor xor_17 (xor_17_out, adder_2_to_adder_3, tristate_A_to_adder_3);
  or or_75 (adder_3_to_adder_4, and_133_out, and_134_out);
  and and_134 (and_134_out, xor_17_out, tristate_B_to_adder_3);
  xor xor_18 (_4s_place, xor_17_out, tristate_B_to_adder_3);
  and and_135 (and_135_out, adder_3_to_adder_4, tristate_A_to_adder_4);
  xor xor_19 (xor_19_out, adder_3_to_adder_4, tristate_A_to_adder_4);
  or or_76 (or_76_out, and_135_out, and_136_out);
  and and_136 (and_136_out, xor_19_out, tristate_B_to_adder_4);
  xor xor_20 (_8s_place, xor_19_out, tristate_B_to_adder_4);
  not not_77 (not_77_out, ram_to_bus);
  xor xor_21 (xor_21_out, in_53, in_53);
  and and_137 (and_137_out, xor_21_out, not_77_out);
  or or_77 (ram_to_bus_4, and_137_out, and_142_out);
  and and_138 (tristate_A_to_adder_4, run_alu, A4_loader_to_tristate);
  and and_139 (tristate_A_to_adder_8, run_alu, A8_loader_to_tristate);
  and and_140 (tristate_B_to_adder_4, run_alu, B4_out);
  and and_141 (tristate_B_to_adder_8, run_alu, B8_out);
  not not_78 (not_78_out, run_alu);
  not not_79 (not_79_out, reg_A_to_bus);
  not not_80 (not_80_out, bus_to_A);
  not not_81 (not_81_out, bus_to_ram);
  not not_82 (not_82_out, bus_to_mem);
  not not_83 (not_83_out, wr00);
  not not_84 (not_84_out, wr00);
  not not_85 (not_85_out, wr00);
  not not_86 (not_86_out, wr00);
  not not_87 (not_87_out, wr00);
  not not_88 (not_88_out, wr00);
  not not_89 (not_89_out, wr00);
  not not_90 (not_90_out, wr00);
  not not_91 (not_91_out, wr04);
  not not_92 (not_92_out, wr04);
  not not_93 (not_93_out, wr04);
  not not_94 (not_94_out, wr04);
  not not_95 (not_95_out, wr04);
  not not_96 (not_96_out, wr04);
  not not_97 (not_97_out, wr04);
  not not_98 (not_98_out, wr04);
  not not_99 (not_99_out, wr08);
  not not_100 (not_100_out, wr08);
  not not_101 (not_101_out, wr08);
  not not_102 (not_102_out, wr08);
  not not_103 (not_103_out, wr08);
  not not_104 (not_104_out, wr08);
  not not_105 (not_105_out, wr08);
  not not_106 (not_106_out, wr08);
  not not_107 (not_107_out, wr12);
  not not_108 (not_108_out, wr12);
  not not_109 (not_109_out, wr12);
  not not_110 (not_110_out, wr12);
  not not_111 (not_111_out, wr12);
  not not_112 (not_112_out, wr12);
  not not_113 (not_113_out, wr12);
  not not_114 (not_114_out, wr12);
  and and_142 (and_142_out, ram_to_bus, ram_4);
  not not_115 (not_115_out, bus_to_mem);
  not not_116 (not_116_out, bus_to_mem);
  and and_143 (run_alu_out, run_alu, not_78_out);
  and and_144 (A_to_bus_out, reg_A_to_bus, not_79_out);
  and and_145 (bus_to_A_out, bus_to_A, not_80_out);
  and and_146 (bus_to_ram_out, bus_to_ram, not_81_out);
  and and_147 (bus_to_mem_out, bus_to_mem, not_82_out);
  and and_148 (and_148_out, out_201, wr00);
  and and_149 (and_149_out, not_83_out, in_8);
  and and_150 (and_150_out, out_200, wr00);
  and and_151 (and_151_out, not_84_out, in_7);
  and and_152 (and_152_out, out_199, wr00);
  and and_153 (and_153_out, not_85_out, in_6);
  and and_154 (and_154_out, out_198, wr00);
  and and_155 (and_155_out, not_86_out, in_5);
  and and_156 (and_156_out, out_197, wr00);
  and and_157 (and_157_out, not_87_out, in_4);
  and and_158 (and_158_out, out_196, wr00);
  and and_159 (and_159_out, not_88_out, in_3);
  and and_160 (and_160_out, out_195, wr00);
  and and_161 (and_161_out, not_89_out, in_2);
  and and_162 (and_162_out, out_194, wr00);
  and and_163 (and_163_out, not_90_out, in_1);
  and and_164 (and_164_out, out_201, wr04);
  and and_165 (and_165_out, not_91_out, in_40);
  and and_166 (and_166_out, out_200, wr04);
  and and_167 (and_167_out, not_92_out, in_39);
  and and_168 (and_168_out, out_199, wr04);
  and and_169 (and_169_out, not_93_out, in_38);
  and and_170 (and_170_out, out_198, wr04);
  and and_171 (and_171_out, not_94_out, in_37);
  and and_172 (and_172_out, out_197, wr04);
  and and_173 (and_173_out, not_95_out, in_36);
  and and_174 (and_174_out, out_196, wr04);
  and and_175 (and_175_out, not_96_out, in_35);
  and and_176 (and_176_out, out_195, wr04);
  and and_177 (and_177_out, not_97_out, in_34);
  and and_178 (and_178_out, out_194, wr04);
  and and_179 (and_179_out, not_98_out, in_33);
  and and_180 (and_180_out, out_201, wr08);
  and and_181 (and_181_out, not_99_out, in_82);
  and and_182 (and_182_out, out_200, wr08);
  and and_183 (and_183_out, not_100_out, in_81);
  and and_184 (and_184_out, out_199, wr08);
  and and_185 (and_185_out, not_101_out, in_80);
  and and_186 (and_186_out, out_198, wr08);
  and and_187 (and_187_out, not_102_out, in_79);
  and and_188 (and_188_out, out_197, wr08);
  and and_189 (and_189_out, not_103_out, in_78);
  and and_190 (and_190_out, out_196, wr08);
  and and_191 (and_191_out, not_104_out, in_77);
  and and_192 (and_192_out, out_195, wr08);
  and and_193 (and_193_out, not_105_out, in_76);
  and and_194 (and_194_out, out_194, wr08);
  and and_195 (and_195_out, not_106_out, in_75);
  and and_196 (and_196_out, out_201, wr12);
  and and_197 (and_197_out, not_107_out, in_144);
  and and_198 (and_198_out, out_200, wr12);
  and and_199 (and_199_out, not_108_out, in_143);
  and and_200 (and_200_out, out_199, wr12);
  and and_201 (and_201_out, not_109_out, in_142);
  and and_202 (and_202_out, out_198, wr12);
  and and_203 (and_203_out, not_110_out, in_141);
  and and_204 (and_204_out, out_197, wr12);
  and and_205 (and_205_out, not_111_out, in_140);
  and and_206 (and_206_out, out_196, wr12);
  and and_207 (and_207_out, not_112_out, in_139);
  and and_208 (and_208_out, out_195, wr12);
  and and_209 (and_209_out, not_113_out, in_138);
  and and_210 (and_210_out, out_194, wr12);
  and and_211 (and_211_out, not_114_out, in_137);
  xor xor_22 (xor_22_out, in_54, in_54);
  not not_117 (not_117_out, ram_to_bus);
  and and_212 (and_212_out, xor_22_out, not_117_out);
  and and_213 (and_213_out, ram_to_bus, ram_3);
  or or_78 (ram_to_bus_3, and_212_out, and_213_out);
  and and_214 (and_214_out, out_201, bus_to_mem);
  or or_79 (M0_out, and_214_out, and_215_out);
  and and_215 (and_215_out, not_115_out, in_178);
  and and_216 (and_216_out, out_199, bus_to_mem);
  or or_80 (M2_out, and_216_out, and_217_out);
  and and_217 (and_217_out, not_116_out, in_174);
  or or_81 (_00_1_out, and_148_out, and_149_out);
  or or_82 (_00_2_out, and_150_out, and_151_out);
  or or_83 (_00_3_out, and_152_out, and_153_out);
  or or_84 (_00_4_out, and_154_out, and_155_out);
  or or_85 (_00_5_out, and_156_out, and_157_out);
  or or_86 (_00_6_out, and_158_out, and_159_out);
  or or_87 (_00_7_out, and_160_out, and_161_out);
  or or_88 (_00_8_out, and_162_out, and_163_out);
  or or_89 (_04_1_out, and_164_out, and_165_out);
  or or_90 (_04_2_out, and_166_out, and_167_out);
  or or_91 (_04_3_out, and_168_out, and_169_out);
  or or_92 (_04_4_out, and_170_out, and_171_out);
  or or_93 (_04_5_out, and_172_out, and_173_out);
  or or_94 (_04_6_out, and_174_out, and_175_out);
  or or_95 (_04_7_out, and_176_out, and_177_out);
  or or_96 (_04_8_out, and_178_out, and_179_out);
  or or_97 (_08_1_out, and_180_out, and_181_out);
  or or_98 (_08_2_out, and_182_out, and_183_out);
  or or_99 (_08_3_out, and_184_out, and_185_out);
  or or_100 (_08_4_out, and_186_out, and_187_out);
  or or_101 (_08_5_out, and_188_out, and_189_out);
  or or_102 (_08_6_out, and_190_out, and_191_out);
  or or_103 (_08_7_out, and_192_out, and_193_out);
  or or_104 (_08_8_out, and_194_out, and_195_out);
  or or_105 (_12_1_out, and_196_out, and_197_out);
  or or_106 (_12_2_out, and_198_out, and_199_out);
  or or_107 (_12_3_out, and_200_out, and_201_out);
  or or_108 (_12_4_out, and_202_out, and_203_out);
  or or_109 (_12_5_out, and_204_out, and_205_out);
  or or_110 (_12_6_out, and_206_out, and_207_out);
  or or_111 (_12_7_out, and_208_out, and_209_out);
  or or_112 (_12_8_out, and_210_out, and_211_out);
  xor xor_23 (xor_23_out, in_55, in_55);
  not not_118 (not_118_out, carry_out_to_inverter);
  not not_119 (not_119_out, ram_to_bus);
  and and_218 (and_218_out, xor_23_out, not_119_out);
  and and_219 (and_219_out, ram_to_bus, ram_2);
  or or_113 (ram_to_bus_2, and_218_out, and_219_out);
  and and_220 (tristate_A_to_adder_3, run_alu, A3_loader_to_tristate);
  and and_221 (tristate_A_to_adder_7, run_alu, A7_loader_to_tristate);
  and and_222 (tristate_B_to_adder_3, run_alu, B3_out);
  and and_223 (tristate_B_to_adder_7, run_alu, B7_out);
  not not_120 (not_120_out, bus_to_mem);
  not not_121 (not_121_out, bus_to_mem);
  and and_224 (and_224_out, or_76_out, tristate_A_to_adder_5);
  xor xor_24 (xor_24_out, or_76_out, tristate_A_to_adder_5);
  and and_225 (and_225_out, xor_24_out, tristate_B_to_adder_5);
  xor xor_25 (_16s_place, xor_24_out, tristate_B_to_adder_5);
  and and_226 (and_226_out, adder_5_to_adder_6, tristate_A_to_adder_6);
  xor xor_26 (xor_26_out, adder_5_to_adder_6, tristate_A_to_adder_6);
  and and_227 (and_227_out, xor_26_out, tristate_B_to_adder_6);
  xor xor_27 (_32s_place, xor_26_out, tristate_B_to_adder_6);
  and and_228 (and_228_out, adder_6_to_adder_7, tristate_A_to_adder_7);
  xor xor_28 (xor_28_out, adder_6_to_adder_7, tristate_A_to_adder_7);
  and and_229 (and_229_out, xor_28_out, tristate_B_to_adder_7);
  xor xor_29 (_64s_place, xor_28_out, tristate_B_to_adder_7);
  and and_230 (and_230_out, adder_7_to_adder_8, tristate_A_to_adder_8);
  xor xor_30 (xor_30_out, adder_7_to_adder_8, tristate_A_to_adder_8);
  and and_231 (and_231_out, xor_30_out, tristate_B_to_adder_8);
  xor xor_31 (_128s_place, xor_30_out, tristate_B_to_adder_8);
  and and_232 (add_or_subtract_out, add_or_subtract, not_122_out);
  not not_122 (not_122_out, add_or_subtract);
  and and_233 (and_233_out, carry_out_to_inverter, not_118_out);
  and and_234 (and_234_out, and_233_out, add_or_subtract);
  not not_123 (not_123_out, add_or_subtract);
  and and_235 (and_235_out, not_123_out, carry_out_to_inverter);
  and and_236 (bus_to_B_out, bus_to_B, not_124_out);
  not not_124 (not_124_out, bus_to_B);
  and and_237 (ram_to_bus_out, ram_to_bus, not_125_out);
  not not_125 (not_125_out, ram_to_bus);
  and and_238 (bus_to_IR_out, bus_to_IR, not_126_out);
  not not_126 (not_126_out, bus_to_IR);
  and and_239 (and_239_out, out_201, wr01);
  not not_127 (not_127_out, wr01);
  and and_240 (and_240_out, not_127_out, in_16);
  and and_241 (and_241_out, out_200, wr01);
  not not_128 (not_128_out, wr01);
  and and_242 (and_242_out, not_128_out, in_15);
  and and_243 (and_243_out, out_199, wr01);
  not not_129 (not_129_out, wr01);
  and and_244 (and_244_out, not_129_out, in_14);
  and and_245 (and_245_out, out_198, wr01);
  not not_130 (not_130_out, wr01);
  and and_246 (and_246_out, not_130_out, in_13);
  and and_247 (and_247_out, out_197, wr01);
  not not_131 (not_131_out, wr01);
  and and_248 (and_248_out, not_131_out, in_12);
  and and_249 (and_249_out, out_196, wr01);
  not not_132 (not_132_out, wr01);
  and and_250 (and_250_out, not_132_out, in_11);
  and and_251 (and_251_out, out_195, wr01);
  not not_133 (not_133_out, wr01);
  and and_252 (and_252_out, not_133_out, in_10);
  and and_253 (and_253_out, out_194, wr01);
  not not_134 (not_134_out, wr01);
  and and_254 (and_254_out, not_134_out, in_9);
  and and_255 (and_255_out, out_201, wr05);
  not not_135 (not_135_out, wr05);
  and and_256 (and_256_out, not_135_out, in_48);
  and and_257 (and_257_out, out_200, wr05);
  not not_136 (not_136_out, wr05);
  and and_258 (and_258_out, not_136_out, in_47);
  and and_259 (and_259_out, out_199, wr05);
  not not_137 (not_137_out, wr05);
  and and_260 (and_260_out, not_137_out, in_46);
  and and_261 (and_261_out, out_198, wr05);
  not not_138 (not_138_out, wr05);
  and and_262 (and_262_out, not_138_out, in_45);
  and and_263 (and_263_out, out_197, wr05);
  not not_139 (not_139_out, wr05);
  and and_264 (and_264_out, not_139_out, in_44);
  and and_265 (and_265_out, out_196, wr05);
  not not_140 (not_140_out, wr05);
  and and_266 (and_266_out, not_140_out, in_43);
  and and_267 (and_267_out, out_195, wr05);
  not not_141 (not_141_out, wr05);
  and and_268 (and_268_out, not_141_out, in_42);
  and and_269 (and_269_out, out_194, wr05);
  not not_142 (not_142_out, wr05);
  and and_270 (and_270_out, not_142_out, in_41);
  and and_271 (and_271_out, out_201, wr09);
  not not_143 (not_143_out, wr09);
  and and_272 (and_272_out, not_143_out, in_91);
  and and_273 (and_273_out, out_200, wr09);
  not not_144 (not_144_out, wr09);
  and and_274 (and_274_out, not_144_out, in_90);
  and and_275 (and_275_out, out_199, wr09);
  not not_145 (not_145_out, wr09);
  and and_276 (and_276_out, not_145_out, in_89);
  and and_277 (and_277_out, out_198, wr09);
  not not_146 (not_146_out, wr09);
  and and_278 (and_278_out, not_146_out, in_88);
  and and_279 (and_279_out, out_197, wr09);
  not not_147 (not_147_out, wr09);
  and and_280 (and_280_out, not_147_out, in_87);
  and and_281 (and_281_out, out_196, wr09);
  not not_148 (not_148_out, wr09);
  and and_282 (and_282_out, not_148_out, in_86);
  and and_283 (and_283_out, out_195, wr09);
  not not_149 (not_149_out, wr09);
  and and_284 (and_284_out, not_149_out, in_85);
  and and_285 (and_285_out, out_194, wr09);
  not not_150 (not_150_out, wr09);
  and and_286 (and_286_out, not_150_out, in_84);
  and and_287 (and_287_out, out_201, wr13);
  not not_151 (not_151_out, wr13);
  and and_288 (and_288_out, not_151_out, in_152);
  and and_289 (and_289_out, out_200, wr13);
  not not_152 (not_152_out, wr13);
  and and_290 (and_290_out, not_152_out, in_151);
  and and_291 (and_291_out, out_199, wr13);
  not not_153 (not_153_out, wr13);
  and and_292 (and_292_out, not_153_out, in_150);
  and and_293 (and_293_out, out_198, wr13);
  not not_154 (not_154_out, wr13);
  and and_294 (and_294_out, not_154_out, in_149);
  and and_295 (and_295_out, out_197, wr13);
  not not_155 (not_155_out, wr13);
  and and_296 (and_296_out, not_155_out, in_148);
  and and_297 (and_297_out, out_196, wr13);
  not not_156 (not_156_out, wr13);
  and and_298 (and_298_out, not_156_out, in_147);
  and and_299 (and_299_out, out_195, wr13);
  not not_157 (not_157_out, wr13);
  and and_300 (and_300_out, not_157_out, in_146);
  and and_301 (and_301_out, out_194, wr13);
  not not_158 (not_158_out, wr13);
  and and_302 (and_302_out, not_158_out, in_145);
  xor xor_32 (xor_32_out, in_56, in_56);
  and and_303 (and_303_out, out_200, bus_to_mem);
  and and_304 (and_304_out, not_120_out, in_177);
  and and_305 (and_305_out, out_198, bus_to_mem);
  and and_306 (and_306_out, not_121_out, RAM_selector);
  or or_114 (adder_5_to_adder_6, and_224_out, and_225_out);
  or or_115 (adder_6_to_adder_7, and_226_out, and_227_out);
  or or_116 (adder_7_to_adder_8, and_228_out, and_229_out);
  or or_117 (carry_out_to_inverter, and_230_out, and_231_out);
  or or_118 (carry_out, and_234_out, and_235_out);
  or or_119 (_01_1_out, and_239_out, and_240_out);
  or or_120 (_01_2_out, and_241_out, and_242_out);
  or or_121 (_01_3_out, and_243_out, and_244_out);
  or or_122 (_01_4_out, and_245_out, and_246_out);
  or or_123 (_01_5_out, and_247_out, and_248_out);
  or or_124 (_01_6_out, and_249_out, and_250_out);
  or or_125 (_01_7_out, and_251_out, and_252_out);
  or or_126 (_01_8_out, and_253_out, and_254_out);
  or or_127 (_05_1_out, and_255_out, and_256_out);
  or or_128 (_05_2_out, and_257_out, and_258_out);
  or or_129 (_05_3_out, and_259_out, and_260_out);
  or or_130 (_05_4_out, and_261_out, and_262_out);
  or or_131 (_05_5_out, and_263_out, and_264_out);
  or or_132 (_05_6_out, and_265_out, and_266_out);
  or or_133 (_05_7_out, and_267_out, and_268_out);
  or or_134 (_05_8_out, and_269_out, and_270_out);
  or or_135 (_09_1_out, and_271_out, and_272_out);
  or or_136 (_09_2_out, and_273_out, and_274_out);
  or or_137 (_09_3_out, and_275_out, and_276_out);
  or or_138 (_09_4_out, and_277_out, and_278_out);
  or or_139 (_09_5_out, and_279_out, and_280_out);
  or or_140 (_09_6_out, and_281_out, and_282_out);
  or or_141 (_09_7_out, and_283_out, and_284_out);
  or or_142 (_09_8_out, and_285_out, and_286_out);
  or or_143 (_13_1_out, and_287_out, and_288_out);
  or or_144 (_13_2_out, and_289_out, and_290_out);
  or or_145 (_13_3_out, and_291_out, and_292_out);
  or or_146 (_13_4_out, and_293_out, and_294_out);
  or or_147 (_13_5_out, and_295_out, and_296_out);
  or or_148 (_13_6_out, and_297_out, and_298_out);
  or or_149 (_13_7_out, and_299_out, and_300_out);
  or or_150 (_13_8_out, and_301_out, and_302_out);
  not not_159 (not_159_out, ram_to_bus);
  and and_307 (and_307_out, xor_32_out, not_159_out);
  and and_308 (and_308_out, ram_to_bus, ram_1);
  or or_151 (ram_to_bus_1, and_307_out, and_308_out);
  or or_152 (M1_out, and_303_out, and_304_out);
  or or_153 (M3_out, and_305_out, and_306_out);
  and and_309 (tristate_A_to_adder_2, run_alu, A2_loader_to_tristate);
  and and_310 (tristate_A_to_adder_6, run_alu, A6_loader_to_tristate);
  and and_311 (tristate_B_to_adder_2, run_alu, B2_out);
  and and_312 (tristate_B_to_adder_6, run_alu, B6_out);
  LED led_1 (.in(run_alu_out));
  LED led_2 (.in(ram_to_bus_out));
  LED led_3 (.in(bus_to_mem_out));
  LED led_4 (.in(A8_out));
  LED led_5 (.in(B8_out));
  LED led_6 (.in(IR_8_out));
  LED led_7 (.in(_00_8_out));
  LED led_8 (.in(_01_8_out));
  LED led_9 (.in(_02_8_out));
  LED led_10 (.in(_03_8_out));
  LED led_11 (.in(_04_8_out));
  LED led_12 (.in(_05_8_out));
  LED led_13 (.in(_06_8_out));
  LED led_14 (.in(_07_8_out));
  LED led_15 (.in(_08_8_out));
  LED led_16 (.in(_09_8_out));
  LED led_17 (.in(_10_8_out));
  LED led_18 (.in(_11_8_out));
  LED led_19 (.in(_12_8_out));
  LED led_20 (.in(_13_8_out));
  LED led_21 (.in(_14_8_out));
  LED led_22 (.in(_15_8_out));
  not not_160 (not_160_out, IR_to_bus);
  not not_161 (not_161_out, wr02);
  not not_162 (not_162_out, wr02);
  not not_163 (not_163_out, wr02);
  not not_164 (not_164_out, wr02);
  not not_165 (not_165_out, wr02);
  not not_166 (not_166_out, wr02);
  not not_167 (not_167_out, wr02);
  not not_168 (not_168_out, wr02);
  not not_169 (not_169_out, wr06);
  not not_170 (not_170_out, wr06);
  not not_171 (not_171_out, wr06);
  not not_172 (not_172_out, wr06);
  not not_173 (not_173_out, wr06);
  not not_174 (not_174_out, wr06);
  not not_175 (not_175_out, wr06);
  not not_176 (not_176_out, wr06);
  not not_177 (not_177_out, wr10);
  not not_178 (not_178_out, wr10);
  not not_179 (not_179_out, wr10);
  not not_180 (not_180_out, wr10);
  not not_181 (not_181_out, wr10);
  not not_182 (not_182_out, wr10);
  not not_183 (not_183_out, wr10);
  not not_184 (not_184_out, wr10);
  not not_185 (not_185_out, wr14);
  not not_186 (not_186_out, wr14);
  not not_187 (not_187_out, wr14);
  not not_188 (not_188_out, wr14);
  not not_189 (not_189_out, wr14);
  not not_190 (not_190_out, wr14);
  not not_191 (not_191_out, wr14);
  not not_192 (not_192_out, wr14);
  LED led_23 (.in(A7_out));
  LED led_24 (.in(B7_out));
  LED led_25 (.in(IR_7_out));
  LED led_26 (.in(_00_7_out));
  LED led_27 (.in(_01_7_out));
  LED led_28 (.in(_02_7_out));
  LED led_29 (.in(_03_7_out));
  LED led_30 (.in(_04_7_out));
  LED led_31 (.in(_05_7_out));
  LED led_32 (.in(_06_7_out));
  LED led_33 (.in(_07_7_out));
  LED led_34 (.in(_08_7_out));
  LED led_35 (.in(_09_7_out));
  LED led_36 (.in(_10_7_out));
  LED led_37 (.in(_11_7_out));
  LED led_38 (.in(_12_7_out));
  LED led_39 (.in(_13_7_out));
  LED led_40 (.in(_14_7_out));
  LED led_41 (.in(_15_7_out));
  and and_313 (IR_to_bus_out, IR_to_bus, not_160_out);
  and and_314 (and_314_out, out_201, wr02);
  or or_154 (_02_1_out, and_314_out, and_315_out);
  and and_315 (and_315_out, not_161_out, in_24);
  and and_316 (and_316_out, out_200, wr02);
  or or_155 (_02_2_out, and_316_out, and_317_out);
  and and_317 (and_317_out, not_162_out, in_23);
  and and_318 (and_318_out, out_199, wr02);
  or or_156 (_02_3_out, and_318_out, and_319_out);
  and and_319 (and_319_out, not_163_out, in_22);
  and and_320 (and_320_out, out_198, wr02);
  or or_157 (_02_4_out, and_320_out, and_321_out);
  and and_321 (and_321_out, not_164_out, in_21);
  and and_322 (and_322_out, out_197, wr02);
  or or_158 (_02_5_out, and_322_out, and_323_out);
  and and_323 (and_323_out, not_165_out, in_20);
  and and_324 (and_324_out, out_196, wr02);
  or or_159 (_02_6_out, and_324_out, and_325_out);
  and and_325 (and_325_out, not_166_out, in_19);
  and and_326 (and_326_out, out_195, wr02);
  or or_160 (_02_7_out, and_326_out, and_327_out);
  and and_327 (and_327_out, not_167_out, in_18);
  and and_328 (and_328_out, out_194, wr02);
  or or_161 (_02_8_out, and_328_out, and_329_out);
  and and_329 (and_329_out, not_168_out, in_17);
  and and_330 (and_330_out, out_201, wr06);
  or or_162 (_06_1_out, and_330_out, and_331_out);
  and and_331 (and_331_out, not_169_out, in_65);
  and and_332 (and_332_out, out_200, wr06);
  or or_163 (_06_2_out, and_332_out, and_333_out);
  and and_333 (and_333_out, not_170_out, in_64);
  and and_334 (and_334_out, out_199, wr06);
  or or_164 (_06_3_out, and_334_out, and_335_out);
  and and_335 (and_335_out, not_171_out, in_63);
  and and_336 (and_336_out, out_198, wr06);
  or or_165 (_06_4_out, and_336_out, and_337_out);
  and and_337 (and_337_out, not_172_out, in_62);
  and and_338 (and_338_out, out_197, wr06);
  or or_166 (_06_5_out, and_338_out, and_339_out);
  and and_339 (and_339_out, not_173_out, in_61);
  and and_340 (and_340_out, out_196, wr06);
  or or_167 (_06_6_out, and_340_out, and_341_out);
  and and_341 (and_341_out, not_174_out, in_60);
  and and_342 (and_342_out, out_195, wr06);
  or or_168 (_06_7_out, and_342_out, and_343_out);
  and and_343 (and_343_out, not_175_out, in_59);
  and and_344 (and_344_out, out_194, wr06);
  or or_169 (_06_8_out, and_344_out, and_345_out);
  and and_345 (and_345_out, not_176_out, in_58);
  and and_346 (and_346_out, out_201, wr10);
  or or_170 (_10_1_out, and_346_out, and_347_out);
  and and_347 (and_347_out, not_177_out, in_107);
  and and_348 (and_348_out, out_200, wr10);
  or or_171 (_10_2_out, and_348_out, and_349_out);
  and and_349 (and_349_out, not_178_out, in_106);
  and and_350 (and_350_out, out_199, wr10);
  or or_172 (_10_3_out, and_350_out, and_351_out);
  and and_351 (and_351_out, not_179_out, in_105);
  and and_352 (and_352_out, out_198, wr10);
  or or_173 (_10_4_out, and_352_out, and_353_out);
  and and_353 (and_353_out, not_180_out, in_104);
  and and_354 (and_354_out, out_197, wr10);
  or or_174 (_10_5_out, and_354_out, and_355_out);
  and and_355 (and_355_out, not_181_out, in_103);
  and and_356 (and_356_out, out_196, wr10);
  or or_175 (_10_6_out, and_356_out, and_357_out);
  and and_357 (and_357_out, not_182_out, in_102);
  and and_358 (and_358_out, out_195, wr10);
  or or_176 (_10_7_out, and_358_out, and_359_out);
  and and_359 (and_359_out, not_183_out, in_101);
  and and_360 (and_360_out, out_194, wr10);
  or or_177 (_10_8_out, and_360_out, and_361_out);
  and and_361 (and_361_out, not_184_out, in_100);
  and and_362 (and_362_out, out_201, wr14);
  or or_178 (_14_1_out, and_362_out, and_363_out);
  and and_363 (and_363_out, not_185_out, in_161);
  and and_364 (and_364_out, out_200, wr14);
  or or_179 (_14_2_out, and_364_out, and_365_out);
  and and_365 (and_365_out, not_186_out, in_160);
  and and_366 (and_366_out, out_199, wr14);
  or or_180 (_14_3_out, and_366_out, and_367_out);
  and and_367 (and_367_out, not_187_out, in_159);
  and and_368 (and_368_out, out_198, wr14);
  or or_181 (_14_4_out, and_368_out, and_369_out);
  and and_369 (and_369_out, not_188_out, in_158);
  and and_370 (and_370_out, out_197, wr14);
  or or_182 (_14_5_out, and_370_out, and_371_out);
  and and_371 (and_371_out, not_189_out, in_157);
  and and_372 (and_372_out, out_196, wr14);
  or or_183 (_14_6_out, and_372_out, and_373_out);
  and and_373 (and_373_out, not_190_out, in_156);
  and and_374 (and_374_out, out_195, wr14);
  or or_184 (_14_7_out, and_374_out, and_375_out);
  and and_375 (and_375_out, not_191_out, in_155);
  and and_376 (and_376_out, out_194, wr14);
  or or_185 (_14_8_out, and_376_out, and_377_out);
  and and_377 (and_377_out, not_192_out, in_154);
  LED led_42 (.in(add_or_subtract_out));
  LED led_43 (.in(bus_to_ram_out));
  LED led_44 (.in(bus_to_IR_out));
  LED led_45 (.in(A6_out));
  LED led_46 (.in(B6_out));
  LED led_47 (.in(IR_6_out));
  LED led_48 (.in(_00_6_out));
  LED led_49 (.in(_01_6_out));
  LED led_50 (.in(_02_6_out));
  LED led_51 (.in(_03_6_out));
  LED led_52 (.in(_04_6_out));
  LED led_53 (.in(_05_6_out));
  LED led_54 (.in(_06_6_out));
  LED led_55 (.in(_07_6_out));
  LED led_56 (.in(_08_6_out));
  LED led_57 (.in(_09_6_out));
  LED led_58 (.in(_10_6_out));
  LED led_59 (.in(_11_6_out));
  LED led_60 (.in(_12_6_out));
  LED led_61 (.in(_13_6_out));
  LED led_62 (.in(_14_6_out));
  LED led_63 (.in(_15_6_out));
  and and_378 (tristate_A_to_adder_1, run_alu, A1_loader_to_tristate);
  and and_379 (tristate_A_to_adder_5, run_alu, A5_loader_to_tristate);
  and and_380 (tristate_B_to_adder_1, run_alu, B1_out);
  and and_381 (tristate_B_to_adder_5, run_alu, B5_out);
  LED led_64 (.in(carry_out));
  LED led_65 (.in(M3_out));
  LED led_66 (.in(IR_to_bus_out));
  LED led_67 (.in(A4_out));
  LED led_68 (.in(A5_out));
  LED led_69 (.in(B5_out));
  LED led_70 (.in(B4_out));
  LED led_71 (.in(IR_5_out));
  LED led_72 (.in(IR_4_out));
  LED led_73 (.in(_00_5_out));
  LED led_74 (.in(_00_4_out));
  LED led_75 (.in(_01_4_out));
  LED led_76 (.in(_01_5_out));
  LED led_77 (.in(_02_5_out));
  LED led_78 (.in(_02_4_out));
  LED led_79 (.in(_03_5_out));
  LED led_80 (.in(_03_4_out));
  LED led_81 (.in(_04_5_out));
  LED led_82 (.in(_04_4_out));
  LED led_83 (.in(_05_5_out));
  LED led_84 (.in(_05_4_out));
  LED led_85 (.in(_06_4_out));
  LED led_86 (.in(_06_5_out));
  LED led_87 (.in(_07_4_out));
  LED led_88 (.in(_07_5_out));
  LED led_89 (.in(_08_5_out));
  LED led_90 (.in(_08_4_out));
  LED led_91 (.in(_09_5_out));
  LED led_92 (.in(_09_4_out));
  LED led_93 (.in(_10_5_out));
  LED led_94 (.in(_10_4_out));
  LED led_95 (.in(_11_4_out));
  LED led_96 (.in(_11_5_out));
  LED led_97 (.in(_12_5_out));
  LED led_98 (.in(_12_4_out));
  LED led_99 (.in(_13_5_out));
  LED led_100 (.in(_13_4_out));
  LED led_101 (.in(_14_5_out));
  LED led_102 (.in(_14_4_out));
  LED led_103 (.in(_15_4_out));
  LED led_104 (.in(_15_5_out));
  LED led_105 (.in(A_to_bus_out));
  LED led_106 (.in(M2_out));
  LED led_107 (.in(halt));
  LED led_108 (.in(A3_out));
  LED led_109 (.in(B3_out));
  LED led_110 (.in(IR_3_out));
  LED led_111 (.in(_00_3_out));
  LED led_112 (.in(_01_3_out));
  LED led_113 (.in(_02_3_out));
  LED led_114 (.in(_03_3_out));
  LED led_115 (.in(_04_3_out));
  LED led_116 (.in(_05_3_out));
  LED led_117 (.in(_06_3_out));
  LED led_118 (.in(_07_3_out));
  LED led_119 (.in(_08_3_out));
  LED led_120 (.in(_09_3_out));
  LED led_121 (.in(_10_3_out));
  LED led_122 (.in(_11_3_out));
  LED led_123 (.in(_12_3_out));
  LED led_124 (.in(_13_3_out));
  LED led_125 (.in(_14_3_out));
  LED led_126 (.in(_15_3_out));
  and and_382 (and_382_out, out_201, wr03);
  not not_193 (not_193_out, wr03);
  and and_383 (and_383_out, not_193_out, in_32);
  and and_384 (and_384_out, out_200, wr03);
  not not_194 (not_194_out, wr03);
  and and_385 (and_385_out, not_194_out, in_31);
  and and_386 (and_386_out, out_199, wr03);
  not not_195 (not_195_out, wr03);
  and and_387 (and_387_out, not_195_out, in_30);
  and and_388 (and_388_out, out_198, wr03);
  not not_196 (not_196_out, wr03);
  and and_389 (and_389_out, not_196_out, in_29);
  and and_390 (and_390_out, out_197, wr03);
  not not_197 (not_197_out, wr03);
  and and_391 (and_391_out, not_197_out, in_28);
  and and_392 (and_392_out, out_196, wr03);
  not not_198 (not_198_out, wr03);
  and and_393 (and_393_out, not_198_out, in_27);
  and and_394 (and_394_out, out_195, wr03);
  not not_199 (not_199_out, wr03);
  and and_395 (and_395_out, not_199_out, in_26);
  and and_396 (and_396_out, out_194, wr03);
  not not_200 (not_200_out, wr03);
  and and_397 (and_397_out, not_200_out, in_25);
  and and_398 (and_398_out, out_201, wr07);
  not not_201 (not_201_out, wr07);
  and and_399 (and_399_out, not_201_out, in_74);
  and and_400 (and_400_out, out_200, wr07);
  not not_202 (not_202_out, wr07);
  and and_401 (and_401_out, not_202_out, in_73);
  and and_402 (and_402_out, out_199, wr07);
  not not_203 (not_203_out, wr07);
  and and_403 (and_403_out, not_203_out, in_72);
  and and_404 (and_404_out, out_198, wr07);
  not not_204 (not_204_out, wr07);
  and and_405 (and_405_out, not_204_out, in_71);
  and and_406 (and_406_out, out_197, wr07);
  not not_205 (not_205_out, wr07);
  and and_407 (and_407_out, not_205_out, in_70);
  and and_408 (and_408_out, out_196, wr07);
  not not_206 (not_206_out, wr07);
  and and_409 (and_409_out, not_206_out, in_69);
  and and_410 (and_410_out, out_195, wr07);
  not not_207 (not_207_out, wr07);
  and and_411 (and_411_out, not_207_out, in_68);
  and and_412 (and_412_out, out_194, wr07);
  not not_208 (not_208_out, wr07);
  and and_413 (and_413_out, not_208_out, in_67);
  and and_414 (and_414_out, out_201, wr11);
  not not_209 (not_209_out, wr11);
  and and_415 (and_415_out, not_209_out, in_133);
  and and_416 (and_416_out, out_200, wr11);
  not not_210 (not_210_out, wr11);
  and and_417 (and_417_out, not_210_out, in_132);
  and and_418 (and_418_out, out_199, wr11);
  not not_211 (not_211_out, wr11);
  and and_419 (and_419_out, not_211_out, in_131);
  and and_420 (and_420_out, out_198, wr11);
  not not_212 (not_212_out, wr11);
  and and_421 (and_421_out, not_212_out, in_130);
  and and_422 (and_422_out, out_197, wr11);
  not not_213 (not_213_out, wr11);
  and and_423 (and_423_out, not_213_out, in_129);
  and and_424 (and_424_out, out_196, wr11);
  not not_214 (not_214_out, wr11);
  and and_425 (and_425_out, not_214_out, in_128);
  and and_426 (and_426_out, out_195, wr11);
  not not_215 (not_215_out, wr11);
  and and_427 (and_427_out, not_215_out, in_127);
  and and_428 (and_428_out, out_194, wr11);
  not not_216 (not_216_out, wr11);
  and and_429 (and_429_out, not_216_out, in_126);
  and and_430 (and_430_out, out_201, wr15);
  not not_217 (not_217_out, wr15);
  and and_431 (and_431_out, not_217_out, in_169);
  and and_432 (and_432_out, out_200, wr15);
  not not_218 (not_218_out, wr15);
  and and_433 (and_433_out, not_218_out, in_168);
  and and_434 (and_434_out, out_199, wr15);
  not not_219 (not_219_out, wr15);
  and and_435 (and_435_out, not_219_out, in_167);
  and and_436 (and_436_out, out_198, wr15);
  not not_220 (not_220_out, wr15);
  and and_437 (and_437_out, not_220_out, in_166);
  and and_438 (and_438_out, out_197, wr15);
  not not_221 (not_221_out, wr15);
  and and_439 (and_439_out, not_221_out, in_165);
  and and_440 (and_440_out, out_196, wr15);
  not not_222 (not_222_out, wr15);
  and and_441 (and_441_out, not_222_out, in_164);
  and and_442 (and_442_out, out_195, wr15);
  not not_223 (not_223_out, wr15);
  and and_443 (and_443_out, not_223_out, in_163);
  and and_444 (and_444_out, out_194, wr15);
  not not_224 (not_224_out, wr15);
  and and_445 (and_445_out, not_224_out, in_162);
  LED led_127 (.in(bus_to_A_out));
  LED led_128 (.in(M1_out));
  LED led_129 (.in(A2_out));
  LED led_130 (.in(B2_out));
  LED led_131 (.in(IR_2_out));
  LED led_132 (.in(_00_2_out));
  LED led_133 (.in(_01_2_out));
  LED led_134 (.in(_02_2_out));
  LED led_135 (.in(_03_2_out));
  LED led_136 (.in(_04_2_out));
  LED led_137 (.in(_05_2_out));
  LED led_138 (.in(_06_2_out));
  LED led_139 (.in(_07_2_out));
  LED led_140 (.in(_08_2_out));
  LED led_141 (.in(_09_2_out));
  LED led_142 (.in(_10_2_out));
  LED led_143 (.in(_11_2_out));
  LED led_144 (.in(_12_2_out));
  LED led_145 (.in(_13_2_out));
  LED led_146 (.in(_14_2_out));
  LED led_147 (.in(_15_2_out));
  or or_186 (_03_1_out, and_382_out, and_383_out);
  or or_187 (_03_2_out, and_384_out, and_385_out);
  or or_188 (_03_3_out, and_386_out, and_387_out);
  or or_189 (_03_4_out, and_388_out, and_389_out);
  or or_190 (_03_5_out, and_390_out, and_391_out);
  or or_191 (_03_6_out, and_392_out, and_393_out);
  or or_192 (_03_7_out, and_394_out, and_395_out);
  or or_193 (_03_8_out, and_396_out, and_397_out);
  or or_194 (_07_1_out, and_398_out, and_399_out);
  or or_195 (_07_2_out, and_400_out, and_401_out);
  or or_196 (_07_3_out, and_402_out, and_403_out);
  or or_197 (_07_4_out, and_404_out, and_405_out);
  or or_198 (_07_5_out, and_406_out, and_407_out);
  or or_199 (_07_6_out, and_408_out, and_409_out);
  or or_200 (_07_7_out, and_410_out, and_411_out);
  or or_201 (_07_8_out, and_412_out, and_413_out);
  or or_202 (_11_1_out, and_414_out, and_415_out);
  or or_203 (_11_2_out, and_416_out, and_417_out);
  or or_204 (_11_3_out, and_418_out, and_419_out);
  or or_205 (_11_4_out, and_420_out, and_421_out);
  or or_206 (_11_5_out, and_422_out, and_423_out);
  or or_207 (_11_6_out, and_424_out, and_425_out);
  or or_208 (_11_7_out, and_426_out, and_427_out);
  or or_209 (_11_8_out, and_428_out, and_429_out);
  or or_210 (_15_1_out, and_430_out, and_431_out);
  or or_211 (_15_2_out, and_432_out, and_433_out);
  or or_212 (_15_3_out, and_434_out, and_435_out);
  or or_213 (_15_4_out, and_436_out, and_437_out);
  or or_214 (_15_5_out, and_438_out, and_439_out);
  or or_215 (_15_6_out, and_440_out, and_441_out);
  or or_216 (_15_7_out, and_442_out, and_443_out);
  or or_217 (_15_8_out, and_444_out, and_445_out);
  LED led_148 (.in(bus_to_B_out));
  LED led_149 (.in(M0_out));
  LED led_150 (.in(A1_out));
  LED led_151 (.in(B1_out));
  LED led_152 (.in(IR_1_out));
  LED led_153 (.in(_00_1_out));
  LED led_154 (.in(_01_1_out));
  LED led_155 (.in(_02_1_out));
  LED led_156 (.in(_03_1_out));
  LED led_157 (.in(_04_1_out));
  LED led_158 (.in(_05_1_out));
  LED led_159 (.in(_06_1_out));
  LED led_160 (.in(_07_1_out));
  LED led_161 (.in(_08_1_out));
  LED led_162 (.in(_09_1_out));
  LED led_163 (.in(_10_1_out));
  LED led_164 (.in(_11_1_out));
  LED led_165 (.in(_12_1_out));
  LED led_166 (.in(_13_1_out));
  LED led_167 (.in(_14_1_out));
  LED led_168 (.in(_15_1_out));
  and and_446 (and_446_out, ram_to_bus, RAM_selector);
  and and_447 (and_447_out, and_446_out, and_493_out);
  and and_448 (and_448_out, ram_to_bus, NA3);
  and and_449 (and_449_out, and_448_out, and_495_out);
  and and_450 (and_450_out, bus_to_ram, RAM_selector);
  and and_451 (and_451_out, bus_to_ram, NA3);
  and and_452 (_15_8_en15, in_162, en15);
  and and_453 (_13_8_en13, in_145, en13);
  and and_454 (_11_8_en11, in_126, en11);
  and and_455 (_09_8_en09, in_84, en09);
  and and_456 (_15_7_en15, in_163, en15);
  and and_457 (_13_7_en13, in_146, en13);
  and and_458 (_11_7_en11, in_127, en11);
  and and_459 (_09_7_en09, in_85, en09);
  and and_460 (_15_6_en15, in_164, en15);
  and and_461 (_13_6_en13, in_147, en13);
  and and_462 (_11_6_en11, in_128, en11);
  and and_463 (_09_6_en09, in_86, en09);
  and and_464 (_15_5_en15, in_165, en15);
  and and_465 (_13_5_en13, in_148, en13);
  and and_466 (_11_5_en11, in_129, en11);
  and and_467 (_09_5_en09, in_87, en09);
  and and_468 (_15_4_en15, in_166, en15);
  and and_469 (_13_4_en13, in_149, en13);
  and and_470 (_11_4_en11, in_130, en11);
  and and_471 (_09_4_en09, in_88, en09);
  and and_472 (_15_3_en15, in_167, en15);
  and and_473 (_13_3_en13, in_150, en13);
  and and_474 (_11_3_en11, in_131, en11);
  and and_475 (_09_3_en09, in_89, en09);
  and and_476 (_15_2_en15, in_168, en15);
  and and_477 (_13_2_en13, in_151, en13);
  and and_478 (_11_2_en11, in_132, en11);
  and and_479 (_09_2_en09, in_90, en09);
  and and_480 (_15_1_en15, in_169, en15);
  and and_481 (_13_1_en13, in_152, en13);
  and and_482 (_11_1_en11, in_133, en11);
  and and_483 (_09_1_en09, in_91, en09);
  and and_484 (and_484_out, out_201, bus_to_IR);
  not not_225 (not_225_out, bus_to_IR);
  and and_485 (and_485_out, not_225_out, in_125);
  and and_486 (and_486_out, out_200, bus_to_IR);
  not not_226 (not_226_out, bus_to_IR);
  and and_487 (and_487_out, not_226_out, in_124);
  and and_488 (and_488_out, out_199, bus_to_IR);
  not not_227 (not_227_out, bus_to_IR);
  and and_489 (and_489_out, not_227_out, in_123);
  and and_490 (and_490_out, out_198, bus_to_IR);
  not not_228 (not_228_out, bus_to_IR);
  and and_491 (and_491_out, not_228_out, in_122);
  and and_492 (and_492_out, in_178, and_493_out);
  and and_493 (and_493_out, in_174, in_177);
  and and_494 (en15, and_447_out, and_492_out);
  and and_495 (and_495_out, in_174, in_177);
  and and_496 (and_496_out, in_178, and_495_out);
  and and_497 (en07, and_449_out, and_496_out);
  and and_498 (and_498_out, in_174, in_177);
  and and_499 (and_499_out, in_178, and_498_out);
  and and_500 (and_500_out, and_450_out, and_498_out);
  and and_501 (wr15, and_500_out, and_499_out);
  and and_502 (and_502_out, in_178, and_503_out);
  and and_503 (and_503_out, in_174, in_177);
  and and_504 (and_504_out, and_451_out, and_503_out);
  and and_505 (wr07, and_504_out, and_502_out);
  or or_218 (IR_1_out, and_484_out, and_485_out);
  or or_219 (IR_2_out, and_486_out, and_487_out);
  or or_220 (IR_3_out, and_488_out, and_489_out);
  or or_221 (IR_4_out, and_490_out, and_491_out);
  xor xor_33 (IR_5_out, in_121, in_121);
  xor xor_34 (IR_6_out, in_120, in_120);
  xor xor_35 (IR_7_out, in_119, in_119);
  xor xor_36 (IR_8_out, in_118, in_118);
  and and_506 (and_506_out, ram_to_bus, RAM_selector);
  and and_507 (and_507_out, ram_to_bus, NA3);
  and and_508 (_14_8_en14, in_154, en14);
  and and_509 (_12_8_en12, in_137, en12);
  and and_510 (_10_8_en10, in_100, en10);
  and and_511 (_08_8_en08, in_75, en08);
  and and_512 (_14_7_en14, in_155, en14);
  and and_513 (_12_7_en12, in_138, en12);
  and and_514 (_10_7_en10, in_101, en10);
  and and_515 (_08_7_en08, in_76, en08);
  and and_516 (_14_6_en14, in_156, en14);
  and and_517 (_12_6_en12, in_139, en12);
  and and_518 (_10_6_en10, in_102, en10);
  and and_519 (_08_6_en08, in_77, en08);
  and and_520 (_14_5_en14, in_157, en14);
  and and_521 (_12_5_en12, in_140, en12);
  and and_522 (_10_5_en10, in_103, en10);
  and and_523 (_08_5_en08, in_78, en08);
  and and_524 (_14_4_en14, in_158, en14);
  and and_525 (_12_4_en12, in_141, en12);
  and and_526 (_10_4_en10, in_104, en10);
  and and_527 (_08_4_en08, in_79, en08);
  and and_528 (_14_3_en14, in_159, en14);
  and and_529 (_12_3_en12, in_142, en12);
  and and_530 (_10_3_en10, in_105, en10);
  and and_531 (_08_3_en08, in_80, en08);
  and and_532 (_14_2_en14, in_160, en14);
  and and_533 (_12_2_en12, in_143, en12);
  and and_534 (_10_2_en10, in_106, en10);
  and and_535 (_08_2_en08, in_81, en08);
  and and_536 (_14_1_en14, in_161, en14);
  and and_537 (_12_1_en12, in_144, en12);
  and and_538 (_10_1_en10, in_107, en10);
  and and_539 (_08_1_en08, in_82, en08);
  and and_540 (and_540_out, in_174, in_177);
  and and_541 (and_541_out, and_506_out, and_540_out);
  and and_542 (en14, and_541_out, and_562_out);
  and and_543 (and_543_out, in_174, in_177);
  and and_544 (and_544_out, and_507_out, and_543_out);
  and and_545 (en06, and_544_out, and_563_out);
  and and_546 (and_546_out, bus_to_ram, RAM_selector);
  and and_547 (and_547_out, in_174, in_177);
  and and_548 (and_548_out, and_546_out, and_547_out);
  and and_549 (wr14, and_548_out, and_564_out);
  and and_550 (and_550_out, in_174, in_177);
  and and_551 (and_551_out, bus_to_ram, NA3);
  and and_552 (and_552_out, and_551_out, and_550_out);
  and and_553 (wr06, and_552_out, and_565_out);
  and and_554 (and_554_out, _15_8_en15, in_178);
  and and_555 (and_555_out, _15_7_en15, in_178);
  and and_556 (and_556_out, _15_6_en15, in_178);
  and and_557 (and_557_out, _15_5_en15, in_178);
  and and_558 (and_558_out, _15_4_en15, in_178);
  and and_559 (and_559_out, _15_3_en15, in_178);
  and and_560 (and_560_out, _15_2_en15, in_178);
  and and_561 (and_561_out, _15_1_en15, in_178);
  not not_229 (not_229_out, in_191);
  not not_230 (not_230_out, in_193);
  not not_231 (not_231_out, in_191);
  and and_562 (and_562_out, NA0, and_540_out);
  and and_563 (and_563_out, NA0, and_543_out);
  and and_564 (and_564_out, NA0, and_547_out);
  and and_565 (and_565_out, NA0, and_550_out);
  not not_232 (not_232_out, in_178);
  and and_566 (and_566_out, not_232_out, _14_8_en14);
  or or_222 (or_222_out, and_554_out, and_566_out);
  and and_567 (and_567_out, or_222_out, in_177);
  not not_233 (not_233_out, in_178);
  and and_568 (and_568_out, not_233_out, _14_7_en14);
  or or_223 (or_223_out, and_555_out, and_568_out);
  and and_569 (and_569_out, or_223_out, in_177);
  not not_234 (not_234_out, in_178);
  and and_570 (and_570_out, not_234_out, _14_6_en14);
  or or_224 (or_224_out, and_556_out, and_570_out);
  and and_571 (and_571_out, or_224_out, in_177);
  not not_235 (not_235_out, in_178);
  and and_572 (and_572_out, not_235_out, _14_5_en14);
  or or_225 (or_225_out, and_557_out, and_572_out);
  and and_573 (and_573_out, or_225_out, in_177);
  not not_236 (not_236_out, in_178);
  and and_574 (and_574_out, not_236_out, _14_4_en14);
  or or_226 (or_226_out, and_558_out, and_574_out);
  and and_575 (and_575_out, or_226_out, in_177);
  not not_237 (not_237_out, in_178);
  and and_576 (and_576_out, not_237_out, _14_3_en14);
  or or_227 (or_227_out, and_559_out, and_576_out);
  and and_577 (and_577_out, or_227_out, in_177);
  not not_238 (not_238_out, in_178);
  and and_578 (and_578_out, not_238_out, _14_2_en14);
  or or_228 (or_228_out, and_560_out, and_578_out);
  and and_579 (and_579_out, or_228_out, in_177);
  not not_239 (not_239_out, in_178);
  and and_580 (and_580_out, not_239_out, _14_1_en14);
  or or_229 (or_229_out, and_561_out, and_580_out);
  and and_581 (and_581_out, or_229_out, in_177);
  nor nor_1 (nor_1_out, in_193, in_192);
  and and_582 (and_582_out, nor_1_out, in_191);
  nor nor_2 (nor_2_out, in_193, in_192);
  and and_583 (and_583_out, nor_2_out, not_229_out);
  and and_584 (and_584_out, not_230_out, in_192);
  and and_585 (and_585_out, and_584_out, not_231_out);
  and and_586 (and_586_out, ram_to_bus, RAM_selector);
  and and_587 (and_587_out, and_586_out, and_613_out);
  and and_588 (and_588_out, ram_to_bus, NA3);
  and and_589 (and_589_out, and_588_out, and_616_out);
  and and_590 (and_590_out, bus_to_ram, RAM_selector);
  and and_591 (and_591_out, and_590_out, and_620_out);
  and and_592 (and_592_out, bus_to_ram, NA3);
  and and_593 (and_593_out, and_592_out, and_622_out);
  not not_240 (not_240_out, in_178);
  and and_594 (and_594_out, _13_8_en13, in_178);
  or or_230 (or_230_out, and_594_out, and_625_out);
  not not_241 (not_241_out, in_177);
  and and_595 (and_595_out, not_241_out, or_230_out);
  or or_231 (or_231_out, and_567_out, and_595_out);
  not not_242 (not_242_out, in_178);
  and and_596 (and_596_out, _13_7_en13, in_178);
  or or_232 (or_232_out, and_596_out, and_627_out);
  not not_243 (not_243_out, in_177);
  and and_597 (and_597_out, not_243_out, or_232_out);
  or or_233 (or_233_out, and_569_out, and_597_out);
  not not_244 (not_244_out, in_178);
  and and_598 (and_598_out, _13_6_en13, in_178);
  or or_234 (or_234_out, and_598_out, and_629_out);
  not not_245 (not_245_out, in_177);
  and and_599 (and_599_out, not_245_out, or_234_out);
  or or_235 (or_235_out, and_571_out, and_599_out);
  not not_246 (not_246_out, in_178);
  and and_600 (and_600_out, _13_5_en13, in_178);
  or or_236 (or_236_out, and_600_out, and_631_out);
  not not_247 (not_247_out, in_177);
  and and_601 (and_601_out, not_247_out, or_236_out);
  or or_237 (or_237_out, and_573_out, and_601_out);
  not not_248 (not_248_out, in_178);
  and and_602 (and_602_out, _13_4_en13, in_178);
  not not_249 (not_249_out, in_177);
  or or_238 (or_238_out, and_602_out, and_633_out);
  and and_603 (and_603_out, not_249_out, or_238_out);
  or or_239 (or_239_out, and_575_out, and_603_out);
  not not_250 (not_250_out, in_178);
  and and_604 (and_604_out, _13_3_en13, in_178);
  or or_240 (or_240_out, and_604_out, and_635_out);
  not not_251 (not_251_out, in_177);
  and and_605 (and_605_out, not_251_out, or_240_out);
  or or_241 (or_241_out, and_577_out, and_605_out);
  not not_252 (not_252_out, in_178);
  and and_606 (and_606_out, _13_2_en13, in_178);
  not not_253 (not_253_out, in_177);
  or or_242 (or_242_out, and_606_out, and_637_out);
  and and_607 (and_607_out, not_253_out, or_242_out);
  or or_243 (or_243_out, and_579_out, and_607_out);
  not not_254 (not_254_out, in_178);
  and and_608 (and_608_out, _13_1_en13, in_178);
  or or_244 (or_244_out, and_608_out, and_639_out);
  not not_255 (not_255_out, in_177);
  and and_609 (and_609_out, not_255_out, or_244_out);
  or or_245 (or_245_out, and_581_out, and_609_out);
  and and_610 (MC_reset, nor_1_out, and_582_out);
  and and_611 (T0, nor_2_out, and_583_out);
  and and_612 (T2, and_584_out, and_585_out);
  and and_613 (and_613_out, in_174, NA1);
  and and_614 (and_614_out, in_178, and_613_out);
  and and_615 (en13, and_587_out, and_614_out);
  and and_616 (and_616_out, in_174, NA1);
  and and_617 (and_617_out, in_178, and_616_out);
  and and_618 (en05, and_589_out, and_617_out);
  and and_619 (and_619_out, in_178, and_620_out);
  and and_620 (and_620_out, in_174, NA1);
  and and_621 (wr13, and_591_out, and_619_out);
  and and_622 (and_622_out, in_174, NA1);
  and and_623 (and_623_out, in_178, and_622_out);
  and and_624 (wr05, and_593_out, and_623_out);
  and and_625 (and_625_out, not_240_out, _12_8_en12);
  not not_256 (not_256_out, in_174);
  and and_626 (and_626_out, or_231_out, in_174);
  or or_246 (or_246_out, and_626_out, and_648_out);
  and and_627 (and_627_out, not_242_out, _12_7_en12);
  not not_257 (not_257_out, in_174);
  and and_628 (and_628_out, or_233_out, in_174);
  or or_247 (or_247_out, and_628_out, and_651_out);
  and and_629 (and_629_out, not_244_out, _12_6_en12);
  not not_258 (not_258_out, in_174);
  and and_630 (and_630_out, or_235_out, in_174);
  or or_248 (or_248_out, and_630_out, and_654_out);
  and and_631 (and_631_out, not_246_out, _12_5_en12);
  not not_259 (not_259_out, in_174);
  and and_632 (and_632_out, or_237_out, in_174);
  or or_249 (or_249_out, and_632_out, and_657_out);
  and and_633 (and_633_out, not_248_out, _12_4_en12);
  not not_260 (not_260_out, in_174);
  and and_634 (and_634_out, or_239_out, in_174);
  or or_250 (or_250_out, and_634_out, and_660_out);
  and and_635 (and_635_out, not_250_out, _12_3_en12);
  not not_261 (not_261_out, in_174);
  and and_636 (and_636_out, or_241_out, in_174);
  or or_251 (or_251_out, and_636_out, and_663_out);
  and and_637 (and_637_out, not_252_out, _12_2_en12);
  not not_262 (not_262_out, in_174);
  and and_638 (and_638_out, or_243_out, in_174);
  or or_252 (or_252_out, and_638_out, and_666_out);
  and and_639 (and_639_out, not_254_out, _12_1_en12);
  not not_263 (not_263_out, in_174);
  and and_640 (and_640_out, or_245_out, in_174);
  or or_253 (or_253_out, and_640_out, and_669_out);
  xnor xnor_1 (xnor_1_out, in_189, in_189);
  not not_264 (MC_0_mux, in_193);
  and and_641 (and_641_out, in_193, in_192);
  not not_265 (not_265_out, in_192);
  not not_266 (not_266_out, in_191);
  not not_267 (not_267_out, in_191);
  and and_642 (and_642_out, ram_to_bus, RAM_selector);
  and and_643 (and_643_out, ram_to_bus, NA3);
  and and_644 (and_644_out, bus_to_ram, RAM_selector);
  and and_645 (and_645_out, bus_to_ram, NA3);
  not not_268 (not_268_out, in_178);
  and and_646 (and_646_out, _11_8_en11, in_178);
  and and_647 (and_647_out, not_268_out, _10_8_en10);
  or or_254 (or_254_out, and_646_out, and_647_out);
  and and_648 (and_648_out, not_256_out, or_262_out);
  not not_269 (not_269_out, in_178);
  and and_649 (and_649_out, _11_7_en11, in_178);
  and and_650 (and_650_out, not_269_out, _10_7_en10);
  or or_255 (or_255_out, and_649_out, and_650_out);
  and and_651 (and_651_out, not_257_out, or_263_out);
  not not_270 (not_270_out, in_178);
  and and_652 (and_652_out, not_270_out, _10_6_en10);
  and and_653 (and_653_out, _11_6_en11, in_178);
  or or_256 (or_256_out, and_653_out, and_652_out);
  and and_654 (and_654_out, not_258_out, or_264_out);
  not not_271 (not_271_out, in_178);
  and and_655 (and_655_out, _11_5_en11, in_178);
  and and_656 (and_656_out, not_271_out, _10_5_en10);
  or or_257 (or_257_out, and_655_out, and_656_out);
  and and_657 (and_657_out, not_259_out, or_265_out);
  not not_272 (not_272_out, in_178);
  and and_658 (and_658_out, not_272_out, _10_4_en10);
  and and_659 (and_659_out, _11_4_en11, in_178);
  or or_258 (or_258_out, and_659_out, and_658_out);
  and and_660 (and_660_out, not_260_out, or_266_out);
  not not_273 (not_273_out, in_178);
  and and_661 (and_661_out, _11_3_en11, in_178);
  and and_662 (and_662_out, not_273_out, _10_3_en10);
  or or_259 (or_259_out, and_661_out, and_662_out);
  and and_663 (and_663_out, not_261_out, or_267_out);
  not not_274 (not_274_out, in_178);
  and and_664 (and_664_out, _11_2_en11, in_178);
  and and_665 (and_665_out, not_274_out, _10_2_en10);
  or or_260 (or_260_out, and_664_out, and_665_out);
  and and_666 (and_666_out, not_262_out, or_268_out);
  not not_275 (not_275_out, in_178);
  and and_667 (and_667_out, not_275_out, _10_1_en10);
  and and_668 (and_668_out, _11_1_en11, in_178);
  or or_261 (or_261_out, and_668_out, and_667_out);
  and and_669 (and_669_out, not_263_out, or_269_out);
  xor xor_37 (MC_1_mux, in_193, in_192);
  xor xor_38 (MC_2_mux, and_641_out, in_191);
  and and_670 (and_670_out, in_193, not_265_out);
  and and_671 (T1, and_670_out, and_672_out);
  and and_672 (and_672_out, and_670_out, not_266_out);
  and and_673 (and_673_out, in_193, in_192);
  and and_674 (T3, and_673_out, and_675_out);
  and and_675 (and_675_out, and_673_out, not_267_out);
  and and_676 (and_676_out, in_174, NA1);
  and and_677 (and_677_out, and_642_out, and_676_out);
  and and_678 (en12, and_677_out, and_715_out);
  and and_679 (and_679_out, in_174, NA1);
  and and_680 (and_680_out, and_643_out, and_679_out);
  and and_681 (en04, and_680_out, and_716_out);
  and and_682 (and_682_out, in_174, NA1);
  and and_683 (and_683_out, and_644_out, and_682_out);
  and and_684 (wr12, and_683_out, and_717_out);
  and and_685 (and_685_out, in_174, NA1);
  and and_686 (and_686_out, and_645_out, and_685_out);
  and and_687 (wr04, and_686_out, and_718_out);
  and and_688 (and_688_out, _09_8_en09, in_178);
  not not_276 (not_276_out, in_177);
  and and_689 (and_689_out, or_254_out, in_177);
  and and_690 (and_690_out, not_276_out, or_270_out);
  or or_262 (or_262_out, and_689_out, and_690_out);
  and and_691 (and_691_out, _09_7_en09, in_178);
  not not_277 (not_277_out, in_177);
  and and_692 (and_692_out, or_255_out, in_177);
  and and_693 (and_693_out, not_277_out, or_271_out);
  or or_263 (or_263_out, and_692_out, and_693_out);
  and and_694 (and_694_out, _09_6_en09, in_178);
  not not_278 (not_278_out, in_177);
  and and_695 (and_695_out, or_256_out, in_177);
  and and_696 (and_696_out, not_278_out, or_272_out);
  or or_264 (or_264_out, and_695_out, and_696_out);
  and and_697 (and_697_out, _09_5_en09, in_178);
  not not_279 (not_279_out, in_177);
  and and_698 (and_698_out, or_257_out, in_177);
  and and_699 (and_699_out, not_279_out, or_273_out);
  or or_265 (or_265_out, and_698_out, and_699_out);
  and and_700 (and_700_out, _09_4_en09, in_178);
  not not_280 (not_280_out, in_177);
  and and_701 (and_701_out, or_258_out, in_177);
  and and_702 (and_702_out, not_280_out, or_274_out);
  or or_266 (or_266_out, and_701_out, and_702_out);
  and and_703 (and_703_out, _09_3_en09, in_178);
  not not_281 (not_281_out, in_177);
  and and_704 (and_704_out, or_259_out, in_177);
  and and_705 (and_705_out, not_281_out, or_275_out);
  or or_267 (or_267_out, and_704_out, and_705_out);
  and and_706 (and_706_out, _09_2_en09, in_178);
  not not_282 (not_282_out, in_177);
  and and_707 (and_707_out, or_260_out, in_177);
  and and_708 (and_708_out, not_282_out, or_276_out);
  or or_268 (or_268_out, and_707_out, and_708_out);
  and and_709 (and_709_out, _09_1_en09, in_178);
  not not_283 (not_283_out, in_177);
  and and_710 (and_710_out, or_261_out, in_177);
  and and_711 (and_711_out, not_283_out, or_277_out);
  or or_269 (or_269_out, and_710_out, and_711_out);
  and and_712 (and_712_out, xnor_1_out, in_190);
  xor xor_39 (PC_0_mux, xnor_1_out, in_190);
  and and_713 (and_713_out, and_712_out, in_189);
  xor xor_40 (PC_1_mux, and_712_out, in_189);
  and and_714 (and_714_out, and_713_out, in_187);
  xor xor_41 (PC_2_mux, and_713_out, in_187);
  xor xor_42 (PC_3_mux, and_714_out, in_186);
  and and_715 (and_715_out, NA0, and_676_out);
  and and_716 (and_716_out, NA0, and_679_out);
  and and_717 (and_717_out, NA0, and_682_out);
  and and_718 (and_718_out, NA0, and_685_out);
  not not_284 (not_284_out, in_178);
  and and_719 (and_719_out, not_284_out, _08_8_en08);
  or or_270 (or_270_out, and_688_out, and_719_out);
  and and_720 (and_720_out, or_246_out, RAM_selector);
  not not_285 (not_285_out, in_178);
  and and_721 (and_721_out, not_285_out, _08_7_en08);
  or or_271 (or_271_out, and_691_out, and_721_out);
  and and_722 (and_722_out, or_247_out, RAM_selector);
  not not_286 (not_286_out, in_178);
  and and_723 (and_723_out, not_286_out, _08_6_en08);
  or or_272 (or_272_out, and_694_out, and_723_out);
  and and_724 (and_724_out, or_248_out, RAM_selector);
  not not_287 (not_287_out, in_178);
  and and_725 (and_725_out, not_287_out, _08_5_en08);
  or or_273 (or_273_out, and_697_out, and_725_out);
  and and_726 (and_726_out, or_249_out, RAM_selector);
  not not_288 (not_288_out, in_178);
  and and_727 (and_727_out, not_288_out, _08_4_en08);
  or or_274 (or_274_out, and_700_out, and_727_out);
  and and_728 (and_728_out, or_250_out, RAM_selector);
  not not_289 (not_289_out, in_178);
  and and_729 (and_729_out, not_289_out, _08_3_en08);
  or or_275 (or_275_out, and_703_out, and_729_out);
  and and_730 (and_730_out, or_251_out, RAM_selector);
  not not_290 (not_290_out, in_178);
  and and_731 (and_731_out, not_290_out, _08_2_en08);
  or or_276 (or_276_out, and_706_out, and_731_out);
  and and_732 (and_732_out, or_252_out, RAM_selector);
  not not_291 (not_291_out, in_178);
  and and_733 (and_733_out, not_291_out, _08_1_en08);
  or or_277 (or_277_out, and_709_out, and_733_out);
  and and_734 (and_734_out, or_253_out, RAM_selector);
  not not_292 (not_292_out, halt);
  not not_293 (not_293_out, halt);
  not not_294 (not_294_out, halt);
  not not_295 (not_295_out, halt);
  not not_296 (not_296_out, MC_reset);
  not not_297 (not_297_out, MC_reset);
  not not_298 (not_298_out, MC_reset);
  not not_299 (not_299_out, MC_reset);
  not not_300 (not_300_out, MC_reset);
  not not_301 (not_301_out, MC_reset);
  and and_735 (and_735_out, ram_to_bus, RAM_selector);
  and and_736 (and_736_out, NA2, in_177);
  and and_737 (and_737_out, and_735_out, and_736_out);
  and and_738 (and_738_out, NA2, in_177);
  and and_739 (and_739_out, ram_to_bus, NA3);
  and and_740 (and_740_out, and_739_out, and_738_out);
  and and_741 (and_741_out, bus_to_ram, RAM_selector);
  and and_742 (and_742_out, and_741_out, and_776_out);
  and and_743 (and_743_out, bus_to_ram, NA3);
  and and_744 (and_744_out, and_743_out, and_778_out);
  not not_302 (not_302_out, in_178);
  and and_745 (and_745_out, _07_8_en07, in_178);
  or or_278 (or_278_out, and_745_out, and_781_out);
  not not_303 (not_303_out, RAM_selector);
  and and_746 (and_746_out, not_303_out, or_317_out);
  or or_279 (ram_8, and_720_out, and_746_out);
  not not_304 (not_304_out, in_178);
  and and_747 (and_747_out, _07_7_en07, in_178);
  or or_280 (or_280_out, and_747_out, and_784_out);
  not not_305 (not_305_out, RAM_selector);
  and and_748 (and_748_out, not_305_out, or_318_out);
  or or_281 (ram_7, and_722_out, and_748_out);
  not not_306 (not_306_out, in_178);
  and and_749 (and_749_out, _07_6_en07, in_178);
  or or_282 (or_282_out, and_749_out, and_787_out);
  not not_307 (not_307_out, RAM_selector);
  and and_750 (and_750_out, not_307_out, or_319_out);
  or or_283 (ram_6, and_724_out, and_750_out);
  not not_308 (not_308_out, in_178);
  and and_751 (and_751_out, _07_5_en07, in_178);
  or or_284 (or_284_out, and_751_out, and_790_out);
  not not_309 (not_309_out, RAM_selector);
  and and_752 (and_752_out, not_309_out, or_320_out);
  or or_285 (ram_5, and_726_out, and_752_out);
  not not_310 (not_310_out, in_178);
  and and_753 (and_753_out, _07_4_en07, in_178);
  or or_286 (or_286_out, and_753_out, and_793_out);
  not not_311 (not_311_out, RAM_selector);
  and and_754 (and_754_out, not_311_out, or_321_out);
  or or_287 (ram_4, and_728_out, and_754_out);
  not not_312 (not_312_out, in_178);
  and and_755 (and_755_out, _07_3_en07, in_178);
  or or_288 (or_288_out, and_755_out, and_796_out);
  not not_313 (not_313_out, RAM_selector);
  and and_756 (and_756_out, not_313_out, or_322_out);
  or or_289 (ram_3, and_730_out, and_756_out);
  not not_314 (not_314_out, in_178);
  and and_757 (and_757_out, _07_2_en07, in_178);
  or or_290 (or_290_out, and_757_out, and_799_out);
  not not_315 (not_315_out, RAM_selector);
  and and_758 (and_758_out, not_315_out, or_323_out);
  or or_291 (ram_2, and_732_out, and_758_out);
  not not_316 (not_316_out, in_178);
  and and_759 (and_759_out, _07_1_en07, in_178);
  or or_292 (or_292_out, and_759_out, and_802_out);
  not not_317 (not_317_out, RAM_selector);
  and and_760 (and_760_out, not_317_out, or_324_out);
  or or_293 (ram_1, and_734_out, and_760_out);
  and and_761 (and_761_out, increment_PC, not_292_out);
  not not_318 (not_318_out, and_761_out);
  not not_319 (not_319_out, and_762_out);
  and and_762 (and_762_out, increment_PC, not_293_out);
  not not_320 (not_320_out, and_763_out);
  and and_763 (and_763_out, increment_PC, not_294_out);
  not not_321 (not_321_out, and_764_out);
  and and_764 (and_764_out, increment_PC, not_295_out);
  and and_765 (and_765_out, not_296_out, MC_reset);
  or or_294 (MC_0_halter, and_765_out, and_766_out);
  and and_766 (and_766_out, not_297_out, MC_0_mux);
  and and_767 (and_767_out, not_298_out, MC_reset);
  or or_295 (MC_1_halter, and_767_out, and_768_out);
  and and_768 (and_768_out, not_299_out, MC_1_mux);
  and and_769 (and_769_out, not_300_out, MC_reset);
  or or_296 (MC_2_halter, and_769_out, and_770_out);
  and and_770 (and_770_out, not_301_out, MC_2_mux);
  and and_771 (and_771_out, in_178, and_736_out);
  and and_772 (en11, and_737_out, and_771_out);
  and and_773 (and_773_out, in_178, and_738_out);
  and and_774 (en03, and_740_out, and_773_out);
  and and_775 (and_775_out, in_178, and_776_out);
  and and_776 (and_776_out, NA2, in_177);
  and and_777 (wr11, and_742_out, and_775_out);
  and and_778 (and_778_out, NA2, in_177);
  and and_779 (and_779_out, in_178, and_778_out);
  and and_780 (wr03, and_744_out, and_779_out);
  and and_781 (and_781_out, not_302_out, _06_8_en06);
  not not_322 (not_322_out, in_177);
  and and_782 (and_782_out, not_322_out, or_305_out);
  and and_783 (and_783_out, or_278_out, in_177);
  or or_297 (or_297_out, and_783_out, and_782_out);
  and and_784 (and_784_out, not_304_out, _06_7_en06);
  not not_323 (not_323_out, in_177);
  and and_785 (and_785_out, or_280_out, in_177);
  and and_786 (and_786_out, not_323_out, or_306_out);
  or or_298 (or_298_out, and_785_out, and_786_out);
  and and_787 (and_787_out, not_306_out, _06_6_en06);
  not not_324 (not_324_out, in_177);
  and and_788 (and_788_out, or_282_out, in_177);
  and and_789 (and_789_out, not_324_out, or_307_out);
  or or_299 (or_299_out, and_788_out, and_789_out);
  and and_790 (and_790_out, not_308_out, _06_5_en06);
  not not_325 (not_325_out, in_177);
  and and_791 (and_791_out, or_284_out, in_177);
  and and_792 (and_792_out, not_325_out, or_308_out);
  or or_300 (or_300_out, and_791_out, and_792_out);
  and and_793 (and_793_out, not_310_out, _06_4_en06);
  not not_326 (not_326_out, in_177);
  and and_794 (and_794_out, not_326_out, or_309_out);
  and and_795 (and_795_out, or_286_out, in_177);
  or or_301 (or_301_out, and_795_out, and_794_out);
  and and_796 (and_796_out, not_312_out, _06_3_en06);
  not not_327 (not_327_out, in_177);
  and and_797 (and_797_out, or_288_out, in_177);
  and and_798 (and_798_out, not_327_out, or_310_out);
  or or_302 (or_302_out, and_797_out, and_798_out);
  and and_799 (and_799_out, not_314_out, _06_2_en06);
  not not_328 (not_328_out, in_177);
  and and_800 (and_800_out, not_328_out, or_311_out);
  and and_801 (and_801_out, or_290_out, in_177);
  or or_303 (or_303_out, and_801_out, and_800_out);
  and and_802 (and_802_out, not_316_out, _06_1_en06);
  not not_329 (not_329_out, in_177);
  and and_803 (and_803_out, not_329_out, or_312_out);
  and and_804 (and_804_out, or_292_out, in_177);
  or or_304 (or_304_out, and_804_out, and_803_out);
  and and_805 (and_805_out, PC_0_mux, and_761_out);
  and and_806 (and_806_out, not_318_out, in_190);
  and and_807 (and_807_out, PC_1_mux, and_762_out);
  and and_808 (and_808_out, not_319_out, in_189);
  and and_809 (and_809_out, PC_2_mux, and_763_out);
  and and_810 (and_810_out, not_320_out, in_187);
  and and_811 (and_811_out, PC_3_mux, and_764_out);
  and and_812 (and_812_out, not_321_out, in_186);
  and and_813 (and_813_out, ram_to_bus, RAM_selector);
  and and_814 (and_814_out, ram_to_bus, NA3);
  and and_815 (and_815_out, bus_to_ram, RAM_selector);
  and and_816 (and_816_out, bus_to_ram, NA3);
  not not_330 (not_330_out, in_178);
  and and_817 (and_817_out, _05_8_en05, in_178);
  and and_818 (and_818_out, not_330_out, _04_8_en04);
  or or_305 (or_305_out, and_817_out, and_818_out);
  and and_819 (and_819_out, or_297_out, in_174);
  not not_331 (not_331_out, in_178);
  and and_820 (and_820_out, _05_7_en05, in_178);
  and and_821 (and_821_out, not_331_out, _04_7_en04);
  or or_306 (or_306_out, and_820_out, and_821_out);
  and and_822 (and_822_out, or_298_out, in_174);
  not not_332 (not_332_out, in_178);
  and and_823 (and_823_out, not_332_out, _04_6_en04);
  and and_824 (and_824_out, _05_6_en05, in_178);
  or or_307 (or_307_out, and_824_out, and_823_out);
  and and_825 (and_825_out, or_299_out, in_174);
  not not_333 (not_333_out, in_178);
  and and_826 (and_826_out, _05_5_en05, in_178);
  and and_827 (and_827_out, not_333_out, _04_5_en04);
  or or_308 (or_308_out, and_826_out, and_827_out);
  and and_828 (and_828_out, or_300_out, in_174);
  not not_334 (not_334_out, in_178);
  and and_829 (and_829_out, not_334_out, _04_4_en04);
  and and_830 (and_830_out, _05_4_en05, in_178);
  or or_309 (or_309_out, and_830_out, and_829_out);
  and and_831 (and_831_out, or_301_out, in_174);
  not not_335 (not_335_out, in_178);
  and and_832 (and_832_out, _05_3_en05, in_178);
  and and_833 (and_833_out, not_335_out, _04_3_en04);
  or or_310 (or_310_out, and_832_out, and_833_out);
  and and_834 (and_834_out, or_302_out, in_174);
  not not_336 (not_336_out, in_178);
  and and_835 (and_835_out, _05_2_en05, in_178);
  and and_836 (and_836_out, not_336_out, _04_2_en04);
  or or_311 (or_311_out, and_835_out, and_836_out);
  and and_837 (and_837_out, or_303_out, in_174);
  not not_337 (not_337_out, in_178);
  and and_838 (and_838_out, _05_1_en05, in_178);
  and and_839 (and_839_out, not_337_out, _04_1_en04);
  or or_312 (or_312_out, and_838_out, and_839_out);
  and and_840 (and_840_out, or_304_out, in_174);
  or or_313 (PC_0_mux_2, and_805_out, and_806_out);
  or or_314 (PC_1_mux_2, and_807_out, and_808_out);
  or or_315 (PC_2_mux_2, and_809_out, and_810_out);
  or or_316 (PC_3_mux_2, and_811_out, and_812_out);
  and and_841 (and_841_out, NA0, and_842_out);
  and and_842 (and_842_out, NA2, in_177);
  and and_843 (and_843_out, and_813_out, and_842_out);
  and and_844 (en10, and_843_out, and_841_out);
  and and_845 (and_845_out, NA0, and_846_out);
  and and_846 (and_846_out, NA2, in_177);
  and and_847 (and_847_out, and_814_out, and_846_out);
  and and_848 (en02, and_847_out, and_845_out);
  and and_849 (and_849_out, NA2, in_177);
  and and_850 (and_850_out, and_815_out, and_849_out);
  and and_851 (wr10, and_850_out, and_871_out);
  and and_852 (and_852_out, NA2, in_177);
  and and_853 (and_853_out, and_816_out, and_852_out);
  and and_854 (wr02, and_853_out, and_872_out);
  and and_855 (and_855_out, _03_8_en03, in_178);
  not not_338 (not_338_out, in_174);
  and and_856 (and_856_out, not_338_out, or_326_out);
  or or_317 (or_317_out, and_819_out, and_856_out);
  and and_857 (and_857_out, _03_7_en03, in_178);
  not not_339 (not_339_out, in_174);
  and and_858 (and_858_out, not_339_out, or_328_out);
  or or_318 (or_318_out, and_822_out, and_858_out);
  and and_859 (and_859_out, _03_6_en03, in_178);
  not not_340 (not_340_out, in_174);
  and and_860 (and_860_out, not_340_out, or_330_out);
  or or_319 (or_319_out, and_825_out, and_860_out);
  and and_861 (and_861_out, _03_5_en03, in_178);
  not not_341 (not_341_out, in_174);
  and and_862 (and_862_out, not_341_out, or_332_out);
  or or_320 (or_320_out, and_828_out, and_862_out);
  and and_863 (and_863_out, _03_4_en03, in_178);
  not not_342 (not_342_out, in_174);
  and and_864 (and_864_out, not_342_out, or_334_out);
  or or_321 (or_321_out, and_831_out, and_864_out);
  and and_865 (and_865_out, _03_3_en03, in_178);
  not not_343 (not_343_out, in_174);
  and and_866 (and_866_out, not_343_out, or_336_out);
  or or_322 (or_322_out, and_834_out, and_866_out);
  and and_867 (and_867_out, _03_2_en03, in_178);
  not not_344 (not_344_out, in_174);
  and and_868 (and_868_out, not_344_out, or_338_out);
  or or_323 (or_323_out, and_837_out, and_868_out);
  and and_869 (and_869_out, _03_1_en03, in_178);
  not not_345 (not_345_out, in_174);
  and and_870 (and_870_out, not_345_out, or_340_out);
  or or_324 (or_324_out, and_840_out, and_870_out);
  and and_871 (and_871_out, NA0, and_849_out);
  and and_872 (and_872_out, NA0, and_852_out);
  not not_346 (not_346_out, in_178);
  and and_873 (and_873_out, not_346_out, _02_8_en02);
  not not_347 (not_347_out, in_177);
  or or_325 (or_325_out, and_855_out, and_873_out);
  and and_874 (and_874_out, or_325_out, in_177);
  or or_326 (or_326_out, and_874_out, and_908_out);
  not not_348 (not_348_out, in_178);
  and and_875 (and_875_out, not_348_out, _02_7_en02);
  or or_327 (or_327_out, and_857_out, and_875_out);
  not not_349 (not_349_out, in_177);
  and and_876 (and_876_out, or_327_out, in_177);
  or or_328 (or_328_out, and_876_out, and_911_out);
  not not_350 (not_350_out, in_178);
  and and_877 (and_877_out, not_350_out, _02_6_en02);
  not not_351 (not_351_out, in_177);
  or or_329 (or_329_out, and_859_out, and_877_out);
  and and_878 (and_878_out, or_329_out, in_177);
  or or_330 (or_330_out, and_878_out, and_914_out);
  not not_352 (not_352_out, in_178);
  and and_879 (and_879_out, not_352_out, _02_5_en02);
  not not_353 (not_353_out, in_177);
  or or_331 (or_331_out, and_861_out, and_879_out);
  and and_880 (and_880_out, or_331_out, in_177);
  or or_332 (or_332_out, and_880_out, and_917_out);
  not not_354 (not_354_out, in_178);
  and and_881 (and_881_out, not_354_out, _02_4_en02);
  or or_333 (or_333_out, and_863_out, and_881_out);
  not not_355 (not_355_out, in_177);
  and and_882 (and_882_out, or_333_out, in_177);
  or or_334 (or_334_out, and_882_out, and_920_out);
  not not_356 (not_356_out, in_178);
  and and_883 (and_883_out, not_356_out, _02_3_en02);
  not not_357 (not_357_out, in_177);
  or or_335 (or_335_out, and_865_out, and_883_out);
  and and_884 (and_884_out, or_335_out, in_177);
  or or_336 (or_336_out, and_884_out, and_923_out);
  not not_358 (not_358_out, in_178);
  and and_885 (and_885_out, not_358_out, _02_2_en02);
  not not_359 (not_359_out, in_177);
  or or_337 (or_337_out, and_867_out, and_885_out);
  and and_886 (and_886_out, or_337_out, in_177);
  or or_338 (or_338_out, and_886_out, and_926_out);
  not not_360 (not_360_out, in_178);
  and and_887 (and_887_out, not_360_out, _02_1_en02);
  or or_339 (or_339_out, and_869_out, and_887_out);
  not not_361 (not_361_out, in_177);
  and and_888 (and_888_out, or_339_out, in_177);
  or or_340 (or_340_out, and_888_out, and_929_out);
  not not_362 (not_362_out, counter_in);
  not not_363 (not_363_out, counter_in);
  not not_364 (not_364_out, counter_in);
  not not_365 (not_365_out, counter_in);
  and and_889 (and_889_out, in_193, halt);
  not not_366 (not_366_out, halt);
  and and_890 (and_890_out, in_192, halt);
  not not_367 (not_367_out, halt);
  and and_891 (and_891_out, in_191, halt);
  not not_368 (not_368_out, halt);
  and and_892 (and_892_out, ram_to_bus, RAM_selector);
  and and_893 (and_893_out, NA2, NA1);
  and and_894 (and_894_out, and_892_out, and_893_out);
  and and_895 (en09, and_894_out, and_944_out);
  and and_896 (and_896_out, ram_to_bus, NA3);
  and and_897 (and_897_out, NA2, NA1);
  and and_898 (and_898_out, and_896_out, and_897_out);
  and and_899 (en01, and_898_out, and_945_out);
  and and_900 (and_900_out, bus_to_ram, RAM_selector);
  and and_901 (and_901_out, NA2, NA1);
  and and_902 (and_902_out, and_900_out, and_901_out);
  and and_903 (and_903_out, NA2, NA1);
  and and_904 (and_904_out, bus_to_ram, NA3);
  and and_905 (and_905_out, and_904_out, and_903_out);
  not not_369 (not_369_out, in_178);
  and and_906 (and_906_out, _01_8_en01, in_178);
  and and_907 (and_907_out, not_369_out, _00_8_en00);
  or or_341 (or_341_out, and_906_out, and_907_out);
  and and_908 (and_908_out, not_347_out, or_341_out);
  not not_370 (not_370_out, in_178);
  and and_909 (and_909_out, not_370_out, _00_7_en00);
  and and_910 (and_910_out, _01_7_en01, in_178);
  or or_342 (or_342_out, and_910_out, and_909_out);
  and and_911 (and_911_out, not_349_out, or_342_out);
  not not_371 (not_371_out, in_178);
  and and_912 (and_912_out, _01_6_en01, in_178);
  and and_913 (and_913_out, not_371_out, _00_6_en00);
  or or_343 (or_343_out, and_912_out, and_913_out);
  and and_914 (and_914_out, not_351_out, or_343_out);
  not not_372 (not_372_out, in_178);
  and and_915 (and_915_out, not_372_out, _00_5_en00);
  and and_916 (and_916_out, _01_5_en01, in_178);
  or or_344 (or_344_out, and_916_out, and_915_out);
  and and_917 (and_917_out, not_353_out, or_344_out);
  not not_373 (not_373_out, in_178);
  and and_918 (and_918_out, _01_4_en01, in_178);
  and and_919 (and_919_out, not_373_out, _00_4_en00);
  or or_345 (or_345_out, and_918_out, and_919_out);
  and and_920 (and_920_out, not_355_out, or_345_out);
  not not_374 (not_374_out, in_178);
  and and_921 (and_921_out, not_374_out, _00_3_en00);
  and and_922 (and_922_out, _01_3_en01, in_178);
  or or_346 (or_346_out, and_922_out, and_921_out);
  and and_923 (and_923_out, not_357_out, or_346_out);
  not not_375 (not_375_out, in_178);
  and and_924 (and_924_out, not_375_out, _00_2_en00);
  and and_925 (and_925_out, _01_2_en01, in_178);
  or or_347 (or_347_out, and_925_out, and_924_out);
  and and_926 (and_926_out, not_359_out, or_347_out);
  not not_376 (not_376_out, in_178);
  and and_927 (and_927_out, _01_1_en01, in_178);
  and and_928 (and_928_out, not_376_out, _00_1_en00);
  or or_348 (or_348_out, and_927_out, and_928_out);
  and and_929 (and_929_out, not_361_out, or_348_out);
  and and_930 (and_930_out, out_201, counter_in);
  or or_349 (out_205, and_930_out, and_931_out);
  and and_931 (and_931_out, not_362_out, PC_0_mux_2);
  and and_932 (and_932_out, out_200, counter_in);
  or or_350 (out_204, and_932_out, and_933_out);
  and and_933 (and_933_out, not_363_out, PC_1_mux_2);
  and and_934 (and_934_out, out_199, counter_in);
  or or_351 (out_203, and_934_out, and_935_out);
  and and_935 (and_935_out, not_364_out, PC_2_mux_2);
  and and_936 (and_936_out, out_198, counter_in);
  or or_352 (out_202, and_936_out, and_937_out);
  and and_937 (and_937_out, not_365_out, PC_3_mux_2);
  and and_938 (and_938_out, and_889_out, halt);
  or or_353 (out_208, and_938_out, and_939_out);
  and and_939 (and_939_out, not_366_out, MC_0_halter);
  and and_940 (and_940_out, and_890_out, halt);
  or or_354 (out_207, and_940_out, and_941_out);
  and and_941 (and_941_out, not_367_out, MC_1_halter);
  and and_942 (and_942_out, and_891_out, halt);
  or or_355 (out_206, and_942_out, and_943_out);
  and and_943 (and_943_out, not_368_out, MC_2_halter);
  and and_944 (and_944_out, in_178, and_893_out);
  and and_945 (and_945_out, in_178, and_897_out);
  and and_946 (and_946_out, in_178, and_901_out);
  and and_947 (wr09, and_902_out, and_946_out);
  and and_948 (and_948_out, in_178, and_903_out);
  and and_949 (wr01, and_905_out, and_948_out);
  and and_950 (and_950_out, ram_to_bus, RAM_selector);
  and and_951 (and_951_out, and_950_out, and_988_out);
  and and_952 (and_952_out, ram_to_bus, NA3);
  and and_953 (and_953_out, and_952_out, and_991_out);
  and and_954 (and_954_out, bus_to_ram, RAM_selector);
  and and_955 (and_955_out, bus_to_ram, NA3);
  and and_956 (_07_8_en07, in_67, en07);
  and and_957 (_05_8_en05, in_41, en05);
  and and_958 (_03_8_en03, in_25, en03);
  and and_959 (_01_8_en01, in_9, en01);
  and and_960 (_07_7_en07, in_68, en07);
  and and_961 (_05_7_en05, in_42, en05);
  and and_962 (_03_7_en03, in_26, en03);
  and and_963 (_01_7_en01, in_10, en01);
  and and_964 (_07_6_en07, in_69, en07);
  and and_965 (_05_6_en05, in_43, en05);
  and and_966 (_03_6_en03, in_27, en03);
  and and_967 (_01_6_en01, in_11, en01);
  and and_968 (_07_5_en07, in_70, en07);
  and and_969 (_05_5_en05, in_44, en05);
  and and_970 (_03_5_en03, in_28, en03);
  and and_971 (_01_5_en01, in_12, en01);
  and and_972 (_07_4_en07, in_71, en07);
  and and_973 (_05_4_en05, in_45, en05);
  and and_974 (_03_4_en03, in_29, en03);
  and and_975 (_01_4_en01, in_13, en01);
  and and_976 (_07_3_en07, in_72, en07);
  and and_977 (_05_3_en05, in_46, en05);
  and and_978 (_03_3_en03, in_30, en03);
  and and_979 (_01_3_en01, in_14, en01);
  and and_980 (_07_2_en07, in_73, en07);
  and and_981 (_05_2_en05, in_47, en05);
  and and_982 (_03_2_en03, in_31, en03);
  and and_983 (_01_2_en01, in_15, en01);
  and and_984 (_07_1_en07, in_74, en07);
  and and_985 (_05_1_en05, in_48, en05);
  and and_986 (_03_1_en03, in_32, en03);
  and and_987 (_01_1_en01, in_16, en01);
  not not_377 (not_377_out, in_118);
  and and_988 (and_988_out, NA2, NA1);
  and and_989 (and_989_out, NA0, and_988_out);
  and and_990 (en08, and_951_out, and_989_out);
  and and_991 (and_991_out, NA2, NA1);
  and and_992 (and_992_out, NA0, and_991_out);
  and and_993 (en00, and_953_out, and_992_out);
  and and_994 (and_994_out, NA2, NA1);
  and and_995 (and_995_out, NA0, and_994_out);
  and and_996 (and_996_out, and_954_out, and_994_out);
  and and_997 (wr08, and_996_out, and_995_out);
  and and_998 (and_998_out, NA0, and_999_out);
  and and_999 (and_999_out, NA2, NA1);
  and and_1000 (and_1000_out, and_955_out, and_999_out);
  and and_1001 (wr00, and_1000_out, and_998_out);
  and and_1002 (and_1002_out, in_118, in_119);
  and and_1003 (and_1003_out, in_120, in_121);
  and and_1004 (halt, and_1002_out, and_1003_out);
  and and_1005 (and_1005_out, not_377_out, in_119);
  and and_1006 (and_1006_out, in_120, in_121);
  and and_1007 (and_1007_out, and_1005_out, and_1006_out);
  and and_1008 (_06_8_en06, in_58, en06);
  and and_1009 (_04_8_en04, in_33, en04);
  and and_1010 (_02_8_en02, in_17, en02);
  and and_1011 (_00_8_en00, in_1, en00);
  and and_1012 (_06_7_en06, in_59, en06);
  and and_1013 (_04_7_en04, in_34, en04);
  and and_1014 (_02_7_en02, in_18, en02);
  and and_1015 (_00_7_en00, in_2, en00);
  and and_1016 (_06_6_en06, in_60, en06);
  and and_1017 (_04_6_en04, in_35, en04);
  and and_1018 (_02_6_en02, in_19, en02);
  and and_1019 (_00_6_en00, in_3, en00);
  and and_1020 (_06_5_en06, in_61, en06);
  and and_1021 (_04_5_en04, in_36, en04);
  and and_1022 (_02_5_en02, in_20, en02);
  and and_1023 (_00_5_en00, in_4, en00);
  and and_1024 (_06_4_en06, in_62, en06);
  and and_1025 (_04_4_en04, in_37, en04);
  and and_1026 (_02_4_en02, in_21, en02);
  and and_1027 (_00_4_en00, in_5, en00);
  and and_1028 (_06_3_en06, in_63, en06);
  and and_1029 (_04_3_en04, in_38, en04);
  and and_1030 (_02_3_en02, in_22, en02);
  and and_1031 (_00_3_en00, in_6, en00);
  and and_1032 (_06_2_en06, in_64, en06);
  and and_1033 (_04_2_en04, in_39, en04);
  and and_1034 (_02_2_en02, in_23, en02);
  and and_1035 (_00_2_en00, in_7, en00);
  and and_1036 (_06_1_en06, in_65, en06);
  and and_1037 (_04_1_en04, in_40, en04);
  and and_1038 (_02_1_en02, in_24, en02);
  and and_1039 (_00_1_en00, in_8, en00);
  and and_1040 (and_1040_out, in_118, in_119);
  and and_1041 (and_1041_out, and_1040_out, and_1044_out);
  not not_378 (not_378_out, in_118);
  and and_1042 (and_1042_out, not_378_out, in_119);
  and and_1043 (and_1043_out, and_1042_out, and_1045_out);
  not not_379 (not_379_out, in_121);
  and and_1044 (and_1044_out, in_120, not_379_out);
  not not_380 (not_380_out, in_121);
  and and_1045 (and_1045_out, in_120, not_380_out);
  not not_381 (not_381_out, in_118);
  not not_382 (not_382_out, in_120);
  and and_1046 (and_1046_out, not_382_out, in_121);
  and and_1047 (and_1047_out, in_118, in_119);
  and and_1048 (and_1048_out, and_1047_out, and_1046_out);
  not not_383 (not_383_out, in_120);
  and and_1049 (and_1049_out, not_383_out, in_121);
  and and_1050 (and_1050_out, not_381_out, in_119);
  and and_1051 (and_1051_out, and_1050_out, and_1049_out);
  and and_1052 (and_1052_out, T2, ADD);
  and and_1053 (and_1053_out, T3, ADD);
  not not_384 (not_384_out, in_120);
  and and_1054 (and_1054_out, in_118, in_119);
  and and_1055 (and_1055_out, and_1054_out, and_1063_out);
  not not_385 (not_385_out, in_120);
  not not_386 (not_386_out, in_118);
  and and_1056 (and_1056_out, not_386_out, in_119);
  and and_1057 (and_1057_out, and_1056_out, and_1064_out);
  or or_356 (or_356_out, and_1052_out, T0);
  or or_357 (bus_to_mem, or_356_out, and_1058_out);
  and and_1058 (and_1058_out, T2, LDA);
  or or_358 (bus_to_ram, in_116, in_134);
  or or_359 (or_359_out, and_1053_out, T1);
  or or_360 (ram_to_bus, or_359_out, and_1059_out);
  and and_1059 (and_1059_out, T3, LDA);
  and and_1060 (and_1060_out, T2, LDA);
  or or_361 (IR_to_bus, and_1060_out, and_1061_out);
  and and_1061 (and_1061_out, T2, ADD);
  or or_362 (bus_to_IR, T1, in_171);
  and and_1062 (and_1062_out, T3, LDA);
  or or_363 (bus_to_A, and_1062_out, in_175);
  not not_387 (not_387_out, in_121);
  and and_1063 (and_1063_out, not_384_out, not_387_out);
  not not_388 (not_388_out, in_121);
  and and_1064 (and_1064_out, not_385_out, not_388_out);
  not not_389 (not_389_out, in_119);
  and and_1065 (and_1065_out, in_118, not_389_out);
  not not_390 (not_390_out, in_119);
  not not_391 (not_391_out, in_118);
  and and_1066 (and_1066_out, not_391_out, not_390_out);
  and and_1067 (and_1067_out, in_120, in_121);
  and and_1068 (and_1068_out, and_1065_out, and_1067_out);
  and and_1069 (and_1069_out, in_120, in_121);
  and and_1070 (and_1070_out, and_1066_out, and_1069_out);
  and and_1071 (and_1071_out, T3, ADD);
  and and_1072 (and_1072_out, T3, ADD);
  not not_392 (not_392_out, in_119);
  and and_1073 (and_1073_out, in_118, not_392_out);
  and and_1074 (and_1074_out, in_120, not_395_out);
  and and_1075 (and_1075_out, and_1073_out, and_1074_out);
  not not_393 (not_393_out, in_118);
  not not_394 (not_394_out, in_119);
  and and_1076 (and_1076_out, in_120, not_396_out);
  and and_1077 (and_1077_out, not_393_out, not_394_out);
  and and_1078 (ADD, and_1077_out, and_1076_out);
  or or_364 (reg_A_to_bus, in_57, in_66);
  or or_365 (run_alu, and_1071_out, in_83);
  or or_366 (add_or_subtract, in_117, in_135);
  or or_367 (bus_to_B, and_1072_out, in_153);
  or or_368 (increment_PC, T1, in_170);
  buf or_369 (counter_to_bus, T0);  // OR_Gate
  or or_370 (counter_in, in_173, in_176);
  not not_395 (not_395_out, in_121);
  not not_396 (not_396_out, in_121);
  not not_397 (not_397_out, in_119);
  and and_1079 (and_1079_out, in_118, not_397_out);
  not not_398 (not_398_out, in_118);
  not not_399 (not_399_out, in_119);
  and and_1080 (and_1080_out, not_398_out, not_399_out);
  not not_400 (not_400_out, in_120);
  and and_1081 (and_1081_out, not_400_out, in_121);
  and and_1082 (and_1082_out, and_1079_out, and_1081_out);
  not not_401 (not_401_out, in_120);
  and and_1083 (and_1083_out, not_401_out, in_121);
  and and_1084 (LDA, and_1080_out, and_1083_out);
  not not_402 (not_402_out, in_120);
  not not_403 (not_403_out, in_119);
  and and_1085 (and_1085_out, in_118, not_403_out);
  and and_1086 (and_1086_out, not_402_out, not_407_out);
  and and_1087 (and_1087_out, and_1085_out, and_1086_out);
  not not_404 (not_404_out, in_118);
  not not_405 (not_405_out, in_119);
  not not_406 (not_406_out, in_120);
  and and_1088 (and_1088_out, not_404_out, not_405_out);
  and and_1089 (and_1089_out, not_406_out, not_408_out);
  and and_1090 (and_1090_out, and_1088_out, and_1089_out);
  not not_407 (not_407_out, in_121);
  not not_408 (not_408_out, in_121);

  // Other names for the same wires on the sheet: _00_1_in = in_8; _00_1_mux = in_8; _00_2_in = in_7; _00_2_mux = in_7;
  //   _00_3_in = in_6; _00_3_mux = in_6; _00_4_in = in_5; _00_4_mux = in_5; _00_5_in = in_4; _00_5_mux = in_4;
  //   _00_6_in = in_3; _00_6_mux = in_3; _00_7_in = in_2; _00_7_mux = in_2; _00_8_in = in_1; _00_8_mux = in_1;
  //   _01_1_in = in_16; _01_1_mux = in_16; _01_2_in = in_15; _01_2_mux = in_15; _01_3_in = in_14; _01_3_mux = in_14;
  //   _01_4_in = in_13; _01_4_mux = in_13; _01_5_in = in_12; _01_5_mux = in_12; _01_6_in = in_11; _01_6_mux = in_11;
  //   _01_7_in = in_10; _01_7_mux = in_10; _01_8_in = in_9; _01_8_mux = in_9; _02_1_in = in_24; _02_1_mux = in_24;
  //   _02_2_in = in_23; _02_2_mux = in_23; _02_3_in = in_22; _02_3_mux = in_22; _02_4_in = in_21; _02_4_mux = in_21;
  //   _02_5_in = in_20; _02_5_mux = in_20; _02_6_in = in_19; _02_6_mux = in_19; _02_7_in = in_18; _02_7_mux = in_18;
  //   _02_8_in = in_17; _02_8_mux = in_17; _03_1_in = in_32; _03_1_mux = in_32; _03_2_in = in_31; _03_2_mux = in_31;
  //   _03_3_in = in_30; _03_3_mux = in_30; _03_4_in = in_29; _03_4_mux = in_29; _03_5_in = in_28; _03_5_mux = in_28;
  //   _03_6_in = in_27; _03_6_mux = in_27; _03_7_in = in_26; _03_7_mux = in_26; _03_8_in = in_25; _03_8_mux = in_25;
  //   _04_1_in = in_40; _04_1_mux = in_40; _04_2_in = in_39; _04_2_mux = in_39; _04_3_in = in_38; _04_3_mux = in_38;
  //   _04_4_in = in_37; _04_4_mux = in_37; _04_5_in = in_36; _04_5_mux = in_36; _04_6_in = in_35; _04_6_mux = in_35;
  //   _04_7_in = in_34; _04_7_mux = in_34; _04_8_in = in_33; _04_8_mux = in_33; _05_1_in = in_48; _05_1_mux = in_48;
  //   _05_2_in = in_47; _05_2_mux = in_47; _05_3_in = in_46; _05_3_mux = in_46; _05_4_in = in_45; _05_4_mux = in_45;
  //   _05_5_in = in_44; _05_5_mux = in_44; _05_6_in = in_43; _05_6_mux = in_43; _05_7_in = in_42; _05_7_mux = in_42;
  //   _05_8_in = in_41; _05_8_mux = in_41; _06_1_in = in_65; _06_1_mux = in_65; _06_2_in = in_64; _06_2_mux = in_64;
  //   _06_3_in = in_63; _06_3_mux = in_63; _06_4_in = in_62; _06_4_mux = in_62; _06_5_in = in_61; _06_5_mux = in_61;
  //   _06_6_in = in_60; _06_6_mux = in_60; _06_7_in = in_59; _06_7_mux = in_59; _06_8_in = in_58; _06_8_mux = in_58;
  //   _07_1_in = in_74; _07_1_mux = in_74; _07_2_in = in_73; _07_2_mux = in_73; _07_3_in = in_72; _07_3_mux = in_72;
  //   _07_4_in = in_71; _07_4_mux = in_71; _07_5_in = in_70; _07_5_mux = in_70; _07_6_in = in_69; _07_6_mux = in_69;
  //   _07_7_in = in_68; _07_7_mux = in_68; _07_8_in = in_67; _07_8_mux = in_67; _08_1_in = in_82; _08_1_mux = in_82;
  //   _08_2_in = in_81; _08_2_mux = in_81; _08_3_in = in_80; _08_3_mux = in_80; _08_4_in = in_79; _08_4_mux = in_79;
  //   _08_5_in = in_78; _08_5_mux = in_78; _08_6_in = in_77; _08_6_mux = in_77; _08_7_in = in_76; _08_7_mux = in_76;
  //   _08_8_in = in_75; _08_8_mux = in_75; _09_1_in = in_91; _09_1_mux = in_91; _09_2_in = in_90; _09_2_mux = in_90;
  //   _09_3_in = in_89; _09_3_mux = in_89; _09_4_in = in_88; _09_4_mux = in_88; _09_5_in = in_87; _09_5_mux = in_87;
  //   _09_6_in = in_86; _09_6_mux = in_86; _09_7_in = in_85; _09_7_mux = in_85; _09_8_in = in_84; _09_8_mux = in_84;
  //   _10_1_in = in_107; _10_1_mux = in_107; _10_2_in = in_106; _10_2_mux = in_106; _10_3_in = in_105;
  //   _10_3_mux = in_105; _10_4_in = in_104; _10_4_mux = in_104; _10_5_in = in_103; _10_5_mux = in_103;
  //   _10_6_in = in_102; _10_6_mux = in_102; _10_7_in = in_101; _10_7_mux = in_101; _10_8_in = in_100;
  //   _10_8_mux = in_100; _11_1_in = in_133; _11_1_mux = in_133; _11_2_in = in_132; _11_2_mux = in_132;
  //   _11_3_in = in_131; _11_3_mux = in_131; _11_4_in = in_130; _11_4_mux = in_130; _11_5_in = in_129;
  //   _11_5_mux = in_129; _11_6_in = in_128; _11_6_mux = in_128; _11_7_in = in_127; _11_7_mux = in_127;
  //   _11_8_in = in_126; _11_8_mux = in_126; _12_1_in = in_144; _12_1_mux = in_144; _12_2_in = in_143;
  //   _12_2_mux = in_143; _12_3_in = in_142; _12_3_mux = in_142; _12_4_in = in_141; _12_4_mux = in_141;
  //   _12_5_in = in_140; _12_5_mux = in_140; _12_6_in = in_139; _12_6_mux = in_139; _12_7_in = in_138;
  //   _12_7_mux = in_138; _12_8_in = in_137; _12_8_mux = in_137; _13_1_in = in_152; _13_1_mux = in_152;
  //   _13_2_in = in_151; _13_2_mux = in_151; _13_3_in = in_150; _13_3_mux = in_150; _13_4_in = in_149;
  //   _13_4_mux = in_149; _13_5_in = in_148; _13_5_mux = in_148; _13_6_in = in_147; _13_6_mux = in_147;
  //   _13_7_in = in_146; _13_7_mux = in_146; _13_8_in = in_145; _13_8_mux = in_145; _14_1_in = in_161;
  //   _14_1_mux = in_161; _14_2_in = in_160; _14_2_mux = in_160; _14_3_in = in_159; _14_3_mux = in_159;
  //   _14_4_in = in_158; _14_4_mux = in_158; _14_5_in = in_157; _14_5_mux = in_157; _14_6_in = in_156;
  //   _14_6_mux = in_156; _14_7_in = in_155; _14_7_mux = in_155; _14_8_in = in_154; _14_8_mux = in_154;
  //   _15_1_in = in_169; _15_1_mux = in_169; _15_2_in = in_168; _15_2_mux = in_168; _15_3_in = in_167;
  //   _15_3_mux = in_167; _15_4_in = in_166; _15_4_mux = in_166; _15_5_in = in_165; _15_5_mux = in_165;
  //   _15_6_in = in_164; _15_6_mux = in_164; _15_7_in = in_163; _15_7_mux = in_163; _15_8_in = in_162;
  //   _15_8_mux = in_162; A1_to_loader = in_99; A2_to_loader = in_98; A3_to_loader = in_97; A4_to_loader = in_96;
  //   A5_to_loader = in_95; A6_to_loader = in_94; A7_to_loader = in_93; A8_to_loader = in_92; B1_to_loader = in_115;
  //   B1_to_tristate = B1_out; B2_to_loader = in_114; B2_to_tristate = B2_out; B3_to_loader = in_113;
  //   B3_to_tristate = B3_out; B4_to_loader = in_112; B4_to_tristate = B4_out; B5_to_loader = in_111;
  //   B5_to_tristate = B5_out; B6_to_loader = in_110; B6_to_tristate = B6_out; B7_to_loader = in_109;
  //   B7_to_tristate = B7_out; B8_to_loader = in_108; B8_to_tristate = B8_out; bus_1 = out_201; bus_2 = out_200;
  //   bus_3 = out_199; bus_4 = out_198; bus_5 = out_197; bus_6 = out_196; bus_7 = out_195; bus_8 = out_194;
  //   halt_out = halt; HLT = halt; initial_carry_out = in_136; IR_1_to_mux = in_125; IR_2_to_mux = in_124;
  //   IR_3_to_mux = in_123; IR_4_to_mux = in_122; IR_5_to_mux = in_121; IR_6_to_mux = in_120; IR_7_to_mux = in_119;
  //   IR_8_to_mux = in_118; MC_0 = in_193; MC_0_out = out_208; MC_1 = in_192; MC_1_out = out_207; MC_2 = in_191;
  //   MC_2_out = out_206; PC_0 = in_190; PC_0_out = out_205; PC_1 = in_189; PC_1_out = out_204; PC_2 = in_187;
  //   PC_2_out = out_203; PC_3 = in_186; PC_3_out = out_202; A0 = in_178; M0_mux = in_178; sel0 = in_178; A1 = in_177;
  //   M1_mux = in_177; sel1 = in_177; A2 = in_174; M2_mux = in_174; sel2 = in_174; A3 = RAM_selector;
  //   M3_mux = RAM_selector; sel3 = RAM_selector

  // Notes on the sheet:
  //   to second 4bit adder
  //   carry in
  //   program counter
  //   microinstruction counter
  //   MI4
endmodule
